// Digital circuit CPU_fullScore.dig as structural Verilog
module CPU_fullScore (
  input  [7:0] M,
  input  [7:0] N,
  input  [12:0] progIN,
  input  reset,
  input  progLoad,
  input  start,
  input  result,
  input  clk,
  input  in_19,
  output valid,
  output done,
  output [7:0] \output ,
  output [7:0] Z,
  output [1:0] out_13,
  output [12:0] out_14,
  output [4:0] Instruction,
  output [7:0] out_16,
  output [7:0] out_17,
  output [7:0] out_18,
  output [4:0] Instruction_2,
  output [7:0] Number
);

  wire _10111eq, _10111gt, _10111ls, _11101eq, accAen, accBen, accCen, and_1_out, and_2_out, and_3_out,
       and_4_out, and_5_out, and_6_out, and_7_out, and_8_out, and_9_out, and_13_out, and_14_out, checking,
       cmp, condition, eq, gt, Jump_Op_d, ls, nand_1_out, nand_2_out, nand_3_out, not_1_out, not_3_out,
       not_4_out, or_1_out, or_3_out, or_4_out, or_5_out, or_6_out, or_7_out, or_8_out, or_9_out, or_10_out,
       prime, Q, ready, reset_Out, result_Out, rRamen;
  wire [2:0] en, readA, readB;
  wire [7:0] _17, _18, _19, _20, _21, _22, _24, _25, _26, _27, _28, add_2_s, cache, counter_1_out,
       counter_3_out, data, memory, multiplexer_1_out, multiplexer_2_out, multiplexer_5_out,
       multiplexer_7_out, rAddress, rpRam;
  wire [12:0] dIn, pRAM_d2;
  wire [12:8] pRAM_d1;

  and and_1 (and_1_out, ~ready, reset, ~reset_Out);  // And
  and and_2 (and_2_out, ready, reset_Out);
  and and_3 (and_3_out, ~reset, result, ~result_Out);  // And
  and and_4 (and_4_out, reset, result_Out);
  and and_5 (and_5_out, ~reset, start, ~Q);  // And
  and and_6 (and_6_out, reset, Q);
  LED u_Start (.in(Q));
  and and_7 (and_7_out, ~Instruction[0], ~Instruction[1], ~Instruction[2], ~Instruction[3], ~Instruction[4]);  // And
  LED Idle (.in(and_7_out));
  nand nand_1 (nand_1_out, ~and_1_out, ~and_2_out);  // NAnd
  nand nand_2 (nand_2_out, ~and_3_out, ~and_4_out);  // NAnd
  nand nand_3 (nand_3_out, ~and_5_out, ~and_6_out);  // NAnd
  LED u_Reset (.in(reset_Out));
  T_FF t_ff_1 (.T(nand_1_out), .C(clk), .Q(reset_Out));  // open: nQ
  T_FF t_ff_2 (.T(nand_2_out), .C(clk), .Q(result_Out));  // open: nQ
  T_FF t_ff_3 (.T(nand_3_out), .C(clk), .Q(Q));  // open: nQ
  LED u_Result (.in(result_Out));
  ROM #(.AddrBits(5), .Bits(3)) Read_A (.A(Instruction), .sel(1'b1), .D(readA));
  Add #(.Bits(8)) add_1 (.a(Number), .b(out_17), .c_i(1'b0), .s(_17));  // open: c_o
  Sub #(.Bits(8)) sub_1 (.a(Number), .b(out_17), .c_i(1'b0), .s(_18));  // open: c_o
  Mul #(.Bits(4)) mul_1 (.a(Number[3:0]), .b(out_17[3:0]), .mul(_19));
  Div #(.Bits(8)) div_1 (.a(Number), .b(out_17), .q(_20));  // open: r
  Multiplexer #(.Selector_Bits(2), .Bits(8)) multiplexer_1 (
    .sel({reset, out_13[0]}), .in_0(add_2_s), .in_1(out_14[7:0]), .in_2({8{1'b0}}), .in_3({8{1'b0}}),
    .out(multiplexer_1_out));
  not not_1 (not_1_out, progLoad);
  ROM #(.AddrBits(5), .Bits(3)) Read_B (.A(Instruction), .sel(1'b1), .D(readB));
  Counter #(.Bits(8)) counter_1 (.en(progLoad), .C(clk), .clr(not_1_out), .out(counter_1_out));  // open: ovf
  and and_8 (and_8_out, Instruction[0], ~Instruction[1], ~Instruction[2], Instruction[3], ~Instruction[4]);  // And
  and and_9 (and_9_out, ~valid, clk, Q, ~checking);  // And
  Multiplexer #(.Bits(8)) multiplexer_2 (
    .sel(and_8_out), .in_0(counter_1_out), .in_1(out_14[7:0]), .out(multiplexer_2_out));
  D_FF #(.Bits(13)) d_ff_1 (.D(progIN), .C(~clk), .Q(dIn));  // open: nQ
  D_FF #(.Bits(8)) pc (.D(multiplexer_1_out), .C(and_9_out), .Q(Z));  // open: nQ
  Div #(.Bits(8)) div_2 (.a(Number), .b(out_17), .r(_21));  // open: q
  Comparator #(.Bits(8)) comparator_1 (.a(Number), .b(out_17), .gt(_10111gt), .eq(_10111eq), .lt(_10111ls));
  assign _24 = ~Number;  // Not not_2, 8 bits wide
  not not_3 (not_3_out, clk);
  not not_4 (not_4_out, clk);
  Register #(.Bits(8)) u_cache (.D(data), .C(not_3_out), .en(1'b1), .Q(cache));
  Register #(.Bits(3)) write_remem (.D(en), .C(not_4_out), .en(1'b1));  // open: Q
  Add #(.Bits(8)) add_2 (.a(Z), .b(8'h1), .c_i(1'b0), .s(add_2_s));  // open: c_o
  RAMDualAccess #(.AddrBits(8), .Bits(13)) pRAM (
    .str(progLoad), .C(clk), .ld(and_8_out), .A1(multiplexer_2_out), .Din1(dIn), .A2(Z),
    .D1({pRAM_d1, rpRam}), .D2(pRAM_d2));
  ROM #(.AddrBits(6), .Bits(8)) rom_1 (.A({out_17[2:0], Number[2:0]}), .sel(1'b1), .D(_22));
  or or_1 (or_1_out, checking, reset);
  Multiplexer #(.Bits(13)) multiplexer_3 (
    .sel(or_1_out), .in_0(pRAM_d2), .in_1({13{1'b0}}), .out({Instruction, out_14[7:0]}));
  assign _26 = Number | out_17;  // Or or_2, 8 bits wide
  assign _25 = Number & out_17;  // And and_10, 8 bits wide
  assign _27 = Number ^ out_17;  // XOr xor_1, 8 bits wide
  BarrelShifter #(.Bits(8)) barrelshifter_1 (.in(Number), .shift({1'b0, out_17[2:0]}), .out(_28));
  or or_3 (or_3_out, reset, accAen);
  or or_4 (or_4_out, reset, accBen);
  or or_5 (or_5_out, reset, accCen);
  Multiplexer #(.Selector_Bits(5), .Bits(8)) multiplexer_4 (
    .sel(Instruction), .in_0({8{1'b0}}), .in_1(out_14[7:0]), .in_2(out_14[7:0]), .in_3(out_17),
    .in_4(Number), .in_5(Number), .in_6(out_16), .in_7(M), .in_8(N), .in_9(rpRam), .in_10(memory),
    .in_11(Number), .in_12(out_14[7:0]), .in_13(out_14[7:0]), .in_14(out_14[7:0]), .in_15(out_14[7:0]),
    .in_16(out_14[7:0]), .in_17(_17), .in_18(_18), .in_19(_19), .in_20(_20), .in_21(_21), .in_22(_22),
    .in_23(8'h5), .in_24(_24), .in_25(_25), .in_26(_26), .in_27(_27), .in_28(_28), .in_29(8'h5),
    .in_30({8{1'b0}}), .in_31({8{1'b0}}), .out(data));
  and and_11 (cmp, Instruction[0], Instruction[1], Instruction[2], ~Instruction[3], Instruction[4]);  // And
  and and_12 (prime, Instruction[0], ~Instruction[1], Instruction[2], Instruction[3], Instruction[4]);  // And
  Register #(.Bits(8)) accA (.D(data), .C(clk), .en(or_3_out), .Q(Number));
  Register #(.Bits(8)) accB (.D(data), .C(clk), .en(or_4_out), .Q(out_17));
  Register #(.Bits(8)) regC (.D(data), .C(clk), .en(or_5_out), .Q(out_16));
  ROM #(.AddrBits(8)) rom_2 (.A(Number), .sel(1'b1), .D(_11101eq));
  and and_13 (and_13_out, _10111eq, cmp);
  or or_6 (or_6_out, _11101eq, and_13_out);
  or or_7 (or_7_out, prime, cmp);
  Register equal_flag (.D(or_6_out), .C(clk), .en(or_7_out), .Q(eq));
  Register greater_flag (.D(_10111gt), .C(clk), .en(cmp), .Q(gt));
  Register lesser_flag (.D(_10111ls), .C(clk), .en(cmp), .Q(ls));
  Counter #(.Bits(8)) counter_2 (.en(reset_Out), .C(clk), .clr(ready), .out(rAddress));  // open: ovf
  and and_14 (and_14_out, result_Out, ~done, valid);  // And
  or or_8 (or_8_out, start, reset, result, progLoad);
  Counter #(.Bits(8)) counter_3 (
    .en(and_14_out), .C(clk), .clr(or_8_out), .out({counter_3_out[7:5], done, counter_3_out[3:0]}));  // open: ovf
  Comparator #(.Bits(8)) comparator_2 (.a(rAddress), .b(8'h10), .eq(ready));  // open: gt, lt
  Multiplexer #(.Bits(8)) multiplexer_5 (.sel(reset_Out), .in_0(out_14[7:0]), .in_1(rAddress), .out(multiplexer_5_out));
  or or_9 (or_9_out, eq, gt);
  Multiplexer #(.Selector_Bits(5), .Bits(3)) multiplexer_6 (
    .sel(Instruction), .in_0(3'b101), .in_1(3'b001), .in_2(3'b010), .in_3(3'b001), .in_4(3'b010),
    .in_5(3'b011), .in_6(3'b001), .in_7(3'b011), .in_8(3'b011), .in_9(3'b001), .in_10(3'b001),
    .in_11(3'b100), .in_12(3'b101), .in_13(3'b101), .in_14(3'b101), .in_15(3'b101), .in_16(3'b101),
    .in_17(3'b001), .in_18(3'b001), .in_19(3'b001), .in_20(3'b001), .in_21(3'b001), .in_22(3'b001),
    .in_23(3'b101), .in_24(3'b001), .in_25(3'b001), .in_26(3'b001), .in_27(3'b001), .in_28(3'b001),
    .in_29(3'b101), .in_30(3'b101), .in_31(3'b101), .out(en));
  or or_10 (or_10_out, rRamen, reset_Out);
  Multiplexer #(.Bits(8)) multiplexer_7 (.sel(reset_Out), .in_0(data), .in_1({8{1'b0}}), .out(multiplexer_7_out));
  Multiplexer #(.Selector_Bits(5)) multiplexer_8 (
    .sel(Instruction), .in_0(1'b1), .in_1(1'b0), .in_2(1'b0), .in_3(1'b0), .in_4(1'b0), .in_5(1'b0),
    .in_6(1'b0), .in_7(1'b0), .in_8(1'b0), .in_9(1'b0), .in_10(1'b0), .in_11(1'b0), .in_12(1'b1), .in_13(eq),
    .in_14(gt), .in_15(ls), .in_16(or_9_out), .in_17(1'b0), .in_18(1'b0), .in_19(1'b0), .in_20(1'b0),
    .in_21(1'b0), .in_22(1'b0), .in_23(1'b0), .in_24(1'b0), .in_25(1'b0), .in_26(1'b0), .in_27(1'b0),
    .in_28(1'b0), .in_29(1'b0), .in_30(1'b0), .in_31(1'b0), .out(condition));
  Decoder #(.Selector_Bits(3)) decoder_1 (
    .sel(en), .out_1(accAen), .out_2(accBen), .out_3(accCen), .out_4(rRamen));  // open: out_0, out_5, out_6, out_7
  RAMDualAccess #(.AddrBits(8), .Bits(8)) rRAM (
    .str(or_10_out), .C(clk), .ld(1'b1), .A1(multiplexer_5_out), .Din1(multiplexer_7_out),
    .A2({counter_3_out[7:5], done, counter_3_out[3:0]}), .D1(memory), .D2(\output ));
  and and_15 (valid, Instruction[0], Instruction[1], Instruction[2], Instruction[3], Instruction[4]);
  ROM #(.AddrBits(5)) Jump_Op (.A(Instruction), .sel(1'b1), .D(Jump_Op_d));
  and and_16 (out_13[0], condition, Jump_Op_d);
  and and_17 (checking, in_19, clk);
  Seven_Seg_Hex seven_seg_hex_1 (.d(\output [7:4]), .dp(1'b0));
  Seven_Seg_Hex seven_seg_hex_2 (.d(\output [3:0]), .dp(1'b0));

  assign Instruction_2 = Instruction;
  assign out_13[1] = reset;
  assign out_14[12:8] = Instruction;
  assign out_18 = Number;

  // Other names for the same wires on the sheet: st = done; accAout[7:0] = Number; accBout[7:0] = out_17;
  //   halt = valid; jump = out_13[0]; operand[7:0] = out_14[7:0]; opCode[4:0] = Instruction; pc[7:0] = Z;
  //   pIn[12:0] = progIN; pLoad = progLoad; regCout[7:0] = out_16; result_In = result

  // Notes on the sheet:
  //   test case
  //   State
  //   Input
  //   Reading
  //   Nothing - 0
  //   A - 1
  //   B - 2
  //   C - 3
  //   rRam - 4
  //   Control Unit
  //   10001
  //   10010
  //   10011
  //   10100
  //   In case opcode has to read 
  //   from two sources
  //   contents of Read_A (hex, n*v repeats v):
  //   4*0,1,1,3,0,0,4,4,1,5*0,13*1
  //   Jump
  //   contents of Read_B (hex, n*v repeats v):
  //   0,0,0,2,14*0,6*2,0,4*2
  //   10110
  //   10101
  //   10111
  //   11000
  //   Cache
  //   contents of rom_1 (hex, n*v repeats v):
  //   0,7*1,0,1,2,3,4,5,6,7,0,1,4,9,10,19,24,31,0,1,8,1b,40,7d,d8,157
  //   ,0,1,10,51,100,41,510,961,0,1,20,f3,400,c35,1e60,41a7,0,1,40,2d9
  //   ,1000,3d09,b640,44f1,0,1,80,88b,4000,1312d,44580,c90f7
  //   11001
  //   11010
  //   11011
  //   11100
  //   Register
  //   Alu
  //   flag
  //   11101
  //   contents of rom_2 (hex, n*v repeats v):
  //   0,0,1,1,0,1,0,1,0,0,0,1,0,1,0,0,0,1,0,1,0,0,0,1,5*0,1,0,1,5*0
  //   ,1,0,0,0,1,0,1,0,0,0,1,5*0,1,5*0,1,0,1,5*0,1,0,0,0,1,0,1,5*0,1
  //   ,0,0,0,1,5*0,1,7*0,1,0,0,0,1,0,1,0,0,0,1,0,1,0,0,0,1,13*0,1,0,0,0
  //   ,1,5*0,1,0,1,9*0,1,0,1,5*0,1,5*0,1,0,0,0,1,5*0,1,5*0,1,0,1,9*0
  //   ,1,0,1,0,0,0,1,0,1,11*0,1,11*0,1,0,0,0,1,0,1,0,0,0,1,5*0,1,0,1
  //   ,9*0,1
  //   Memory
  //   enWrite
  //   Nothing - 5
  //   A - 1
  //   B - 2
  //   C - 3
  //   rRam - 4
  //   wannajump?
  //   contents of Jump_Op (hex, n*v repeats v):
  //   12*0,5*1
endmodule

/* Test case 01_P01T01:
M N progIN reset progLoad start result clk valid done output
0 0 0 0 0 0 0 0 0 0 0
0 0 0 0 0 0 0 1 0 0 0
0 0 0 1 0 0 0 0 0 0 0
0 0 0 1 0 0 0 1 0 0 0
0 0 0 0 0 0 0 0 0 0 0
0 0 0 0 0 0 0 1 0 0 0
0 0 0 0 0 0 0 0 0 0 0
0 0 0 0 0 0 0 1 0 0 0
0 0 0 0 0 0 0 0 0 0 0
0 0 0 0 0 0 0 1 0 0 0
0 0 0 0 0 0 0 0 0 0 0
0 0 0 0 0 0 0 1 0 0 0
0 0 0 0 0 0 0 0 0 0 0
0 0 0 0 0 0 0 1 0 0 0
0 0 0 0 0 0 0 0 0 0 0
0 0 0 0 0 0 0 1 0 0 0
0 0 0 0 0 0 0 0 0 0 0
0 0 0 0 0 0 0 1 0 0 0
0 0 0 0 0 0 0 0 0 0 0
0 0 0 0 0 0 0 1 0 0 0
0 0 0 0 0 0 0 0 0 0 0
0 0 0 0 0 0 0 1 0 0 0
0 0 0 0 0 0 0 0 0 0 0
0 0 0 0 0 0 0 1 0 0 0
0 0 0 0 0 0 0 0 0 0 0
0 0 0 0 0 0 0 1 0 0 0
0 0 0 0 0 0 0 0 0 0 0
0 0 0 0 0 0 0 1 0 0 0
0 0 0 0 0 0 0 0 0 0 0
0 0 0 0 0 0 0 1 0 0 0
0 0 0 0 0 0 0 0 0 0 0
0 0 0 0 0 0 0 1 0 0 0
0 0 0 0 0 0 0 0 0 0 0
0 0 0 0 0 0 0 1 0 0 0
0 0 0 0 0 0 0 0 0 0 0
0 0 0 0 0 0 0 1 0 0 0
0 0 0 0 0 0 0 0 0 0 0
0 0 0 0 0 0 0 1 0 0 0
0 0 0 0 0 0 0 0 0 0 0
0 0 0 0 0 0 0 1 0 0 0
0 0 0 0 0 0 0 0 0 0 0
0 0 0 0 0 0 0 1 0 0 0
0 0 271 0 1 0 0 0 0 0 0
0 0 0 0 1 0 0 1 0 0 0
0 0 565 0 1 0 0 0 0 0 0
0 0 0 0 1 0 0 1 0 0 0
0 0 4352 0 1 0 0 0 0 0 0
0 0 0 0 1 0 0 1 0 0 0
0 0 2819 0 1 0 0 0 0 0 0
0 0 0 0 1 0 0 1 0 0 0
0 0 7936 0 1 0 0 0 0 0 0
0 0 0 0 1 0 0 1 0 0 0
0 0 0 0 0 1 0 0 0 0 0
0 0 0 0 0 1 0 1 0 0 0
0 0 0 0 0 0 0 0 x 0 0
0 0 0 0 0 0 0 1 x 0 0
0 0 0 0 0 0 0 0 x 0 0
0 0 0 0 0 0 0 1 x 0 0
0 0 0 0 0 0 0 0 x 0 0
0 0 0 0 0 0 0 1 x 0 0
0 0 0 0 0 0 0 0 x 0 0
0 0 0 0 0 0 0 1 x 0 0
0 0 0 0 0 0 0 0 x 0 0
0 0 0 0 0 0 0 1 x 0 0
0 0 0 0 0 0 0 0 x 0 0
0 0 0 0 0 0 0 1 x 0 0
0 0 0 0 0 0 0 0 x 0 0
0 0 0 0 0 0 0 1 x 0 0
0 0 0 0 0 0 0 0 x 0 0
0 0 0 0 0 0 0 1 x 0 0
0 0 0 0 0 0 0 0 x 0 0
0 0 0 0 0 0 0 1 x 0 0
0 0 0 0 0 0 0 0 x 0 0
0 0 0 0 0 0 0 1 x 0 0
0 0 0 0 0 0 0 0 x 0 0
0 0 0 0 0 0 0 1 x 0 0
0 0 0 0 0 0 0 0 x 0 0
0 0 0 0 0 0 0 1 x 0 0
0 0 0 0 0 0 0 0 x 0 0
0 0 0 0 0 0 0 1 x 0 0
0 0 0 0 0 0 0 0 x 0 0
0 0 0 0 0 0 0 1 x 0 0
0 0 0 0 0 0 0 0 x 0 0
0 0 0 0 0 0 0 1 x 0 0
0 0 0 0 0 0 0 0 x 0 0
0 0 0 0 0 0 0 1 x 0 0
0 0 0 0 0 0 0 0 x 0 0
0 0 0 0 0 0 0 1 x 0 0
0 0 0 0 0 0 0 0 x 0 0
0 0 0 0 0 0 0 1 x 0 0
0 0 0 0 0 0 0 0 x 0 0
0 0 0 0 0 0 0 1 x 0 0
0 0 0 0 0 0 0 0 x 0 0
0 0 0 0 0 0 0 1 x 0 0
0 0 0 0 0 0 0 0 x 0 0
0 0 0 0 0 0 0 1 x 0 0
0 0 0 0 0 0 0 0 x 0 0
0 0 0 0 0 0 0 1 x 0 0
0 0 0 0 0 0 0 0 x 0 0
0 0 0 0 0 0 0 1 x 0 0
0 0 0 0 0 0 0 0 x 0 0
0 0 0 0 0 0 0 1 x 0 0
0 0 0 0 0 0 0 0 x 0 0
0 0 0 0 0 0 0 1 x 0 0
0 0 0 0 0 0 0 0 x 0 0
0 0 0 0 0 0 0 1 1 0 0
0 0 0 0 0 0 1 0 1 0 0
0 0 0 0 0 0 1 1 1 0 0
0 0 0 0 0 0 0 0 1 0 0
0 0 0 0 0 0 0 1 1 0 0
0 0 0 0 0 0 0 0 1 0 0
0 0 0 0 0 0 0 1 1 0 0
0 0 0 0 0 0 0 0 1 0 0
0 0 0 0 0 0 0 1 1 0 68
0 0 0 0 0 0 0 0 1 0 68
0 0 0 0 0 0 0 1 1 0 0
0 0 0 0 0 0 0 0 1 0 0
0 0 0 0 0 0 0 1 1 0 0
0 0 0 0 0 0 0 0 1 0 0
0 0 0 0 0 0 0 1 1 0 0
0 0 0 0 0 0 0 0 1 0 0
0 0 0 0 0 0 0 1 1 0 0
0 0 0 0 0 0 0 0 1 0 0
0 0 0 0 0 0 0 1 1 0 0
0 0 0 0 0 0 0 0 1 0 0
0 0 0 0 0 0 0 1 1 0 0
0 0 0 0 0 0 0 0 1 0 0
0 0 0 0 0 0 0 1 1 0 0
0 0 0 0 0 0 0 0 1 0 0
0 0 0 0 0 0 0 1 1 0 0
0 0 0 0 0 0 0 0 1 0 0
0 0 0 0 0 0 0 1 1 0 0
0 0 0 0 0 0 0 0 1 0 0
0 0 0 0 0 0 0 1 1 0 0
0 0 0 0 0 0 0 0 1 0 0
0 0 0 0 0 0 0 1 1 0 0
0 0 0 0 0 0 0 0 1 0 0
0 0 0 0 0 0 0 1 1 0 0
0 0 0 0 0 0 0 0 1 0 0
0 0 0 0 0 0 0 1 1 1 0
0 0 0 0 0 0 0 0 1 1 0
0 0 0 0 0 0 0 1 1 1 0
0 0 0 0 0 0 0 0 1 1 0
*/

/* Test case 04_P03T1:
M N progIN reset progLoad start result clk valid done output
0 0 0 0 0 0 0 0 x x x
0 0 0 0 0 0 0 1 x x x
0 0 0 1 0 0 0 0 x x x
0 0 0 1 0 0 0 1 0 0 x
0 0 0 0 0 0 0 0 0 0 x
0 0 0 0 0 0 0 1 0 0 x
0 0 0 0 0 0 0 0 0 0 x
0 0 0 0 0 0 0 1 0 0 x
0 0 0 0 0 0 0 0 0 0 x
0 0 0 0 0 0 0 1 0 0 x
0 0 0 0 0 0 0 0 0 0 x
0 0 0 0 0 0 0 1 0 0 x
0 0 0 0 0 0 0 0 0 0 x
0 0 0 0 0 0 0 1 0 0 x
0 0 0 0 0 0 0 0 0 0 x
0 0 0 0 0 0 0 1 0 0 x
0 0 0 0 0 0 0 0 0 0 x
0 0 0 0 0 0 0 1 0 0 x
0 0 0 0 0 0 0 0 0 0 x
0 0 0 0 0 0 0 1 0 0 x
0 0 0 0 0 0 0 0 0 0 x
0 0 0 0 0 0 0 1 0 0 x
0 0 0 0 0 0 0 0 0 0 x
0 0 0 0 0 0 0 1 0 0 x
0 0 0 0 0 0 0 0 0 0 x
0 0 0 0 0 0 0 1 0 0 x
0 0 0 0 0 0 0 0 0 0 x
0 0 0 0 0 0 0 1 0 0 x
0 0 0 0 0 0 0 0 0 0 x
0 0 0 0 0 0 0 1 0 0 x
0 0 0 0 0 0 0 0 0 0 x
0 0 0 0 0 0 0 1 0 0 x
0 0 0 0 0 0 0 0 0 0 x
0 0 0 0 0 0 0 1 0 0 x
0 0 0 0 0 0 0 0 0 0 x
0 0 0 0 0 0 0 1 0 0 x
0 0 0 0 0 0 0 0 0 0 x
0 0 0 0 0 0 0 1 0 0 x
0 0 0 0 0 0 0 0 0 0 x
0 0 0 0 0 0 0 1 0 0 x
0 0 0 0 0 0 0 0 0 0 x
0 0 0 0 0 0 0 1 0 0 x
0 0 0 0 0 0 0 0 0 0 x
0 0 0 0 0 0 0 1 0 0 x
0 0 271 0 1 0 0 0 0 0 x
0 0 271 0 1 0 0 1 0 0 x
0 0 565 0 1 0 0 0 0 0 x
0 0 565 0 1 0 0 1 0 0 x
0 0 2309 0 1 0 0 0 0 0 x
0 0 2309 0 1 0 0 1 0 0 x
0 0 4352 0 1 0 0 0 0 0 x
0 0 4352 0 1 0 0 1 0 0 x
0 0 2818 0 1 0 0 0 0 0 x
0 0 2818 0 1 0 0 1 0 0 x
0 0 2311 0 1 0 0 0 0 0 x
0 0 2311 0 1 0 0 1 0 0 x
0 0 4366 0 1 0 0 0 0 0 x
0 0 4366 0 1 0 0 1 0 0 x
0 0 12 0 1 0 0 0 0 0 x
0 0 12 0 1 0 0 1 0 0 x
0 0 4359 0 1 0 0 0 0 0 x
0 0 4359 0 1 0 0 1 0 0 x
0 0 2819 0 1 0 0 0 0 0 x
0 0 2819 0 1 0 0 1 0 0 x
0 0 7936 0 1 0 0 0 0 0 x
0 0 7936 0 1 0 0 1 0 0 x
0 0 0 0 0 0 0 0 0 0 x
0 0 0 0 0 0 0 1 0 0 x
0 0 0 0 0 0 0 0 0 0 x
0 0 0 0 0 0 0 1 0 0 x
0 0 0 0 0 0 0 0 0 0 x
0 0 0 0 0 0 0 1 0 0 x
0 0 0 0 0 0 0 0 0 0 x
0 0 0 0 0 0 0 1 0 0 x
0 0 0 0 0 0 0 0 0 0 x
0 0 0 0 0 0 0 1 0 0 x
0 0 0 0 0 0 0 0 0 0 x
0 0 0 0 0 0 0 1 0 0 x
0 0 0 0 0 0 0 0 0 0 x
0 0 0 0 0 0 0 1 0 0 x
0 0 0 0 0 0 0 0 0 0 x
0 0 0 0 0 0 0 1 0 0 x
0 0 0 0 0 0 0 0 0 0 x
0 0 0 0 0 0 0 1 0 0 x
0 0 0 0 0 0 0 0 0 0 x
0 0 0 0 0 0 0 1 0 0 x
0 0 0 0 0 0 0 0 0 0 x
0 0 0 0 0 0 0 1 0 0 x
0 0 0 0 0 0 0 0 0 0 x
0 0 0 0 0 0 0 1 0 0 x
0 0 0 0 0 1 0 0 0 0 x
0 0 0 0 0 1 0 1 0 0 x
0 0 0 0 0 0 0 0 x 0 x
0 0 0 0 0 0 0 1 x 0 x
0 0 0 0 0 0 0 0 x 0 x
0 0 0 0 0 0 0 1 x 0 x
0 0 0 0 0 0 0 0 x 0 x
0 0 0 0 0 0 0 1 x 0 x
0 0 0 0 0 0 0 0 x 0 x
0 0 0 0 0 0 0 1 x 0 x
0 0 0 0 0 0 0 0 x 0 x
0 0 0 0 0 0 0 1 x 0 x
0 0 0 0 0 0 0 0 x 0 x
0 0 0 0 0 0 0 1 x 0 x
0 0 0 0 0 0 0 0 x 0 x
0 0 0 0 0 0 0 1 x 0 x
0 0 0 0 0 0 0 0 x 0 x
0 0 0 0 0 0 0 1 x 0 x
0 0 0 0 0 0 0 0 x 0 x
0 0 0 0 0 0 0 1 x 0 x
0 0 0 0 0 0 0 0 x 0 x
0 0 0 0 0 0 0 1 x 0 x
0 0 0 0 0 0 0 0 x 0 x
0 0 0 0 0 0 0 1 x 0 x
0 0 0 0 0 0 0 0 x 0 x
0 0 0 0 0 0 0 1 x 0 x
0 0 0 0 0 0 0 0 x 0 x
0 0 0 0 0 0 0 1 x 0 x
0 0 0 0 0 0 0 0 x 0 x
0 0 0 0 0 0 0 1 x 0 x
0 0 0 0 0 0 0 0 x 0 x
0 0 0 0 0 0 0 1 x 0 x
0 0 0 0 0 0 0 0 x 0 x
0 0 0 0 0 0 0 1 x 0 x
0 0 0 0 0 0 0 0 x 0 x
0 0 0 0 0 0 0 1 x 0 x
0 0 0 0 0 0 0 0 x 0 x
0 0 0 0 0 0 0 1 x 0 x
0 0 0 0 0 0 0 0 x 0 x
0 0 0 0 0 0 0 1 x 0 x
0 0 0 0 0 0 0 0 x 0 x
0 0 0 0 0 0 0 1 x 0 x
0 0 0 0 0 0 0 0 x 0 x
0 0 0 0 0 0 0 1 x 0 x
0 0 0 0 0 0 0 0 x 0 x
0 0 0 0 0 0 0 1 x 0 x
0 0 0 0 0 0 0 0 x 0 x
0 0 0 0 0 0 0 1 x 0 x
0 0 0 0 0 0 0 0 x 0 x
0 0 0 0 0 0 0 1 x 0 x
0 0 0 0 0 0 0 0 x 0 x
0 0 0 0 0 0 0 1 x 0 x
0 0 0 0 0 0 0 0 x 0 x
0 0 0 0 0 0 0 1 1 0 x
0 0 0 0 0 0 1 0 1 0 x
0 0 0 0 0 0 1 1 1 0 0
0 0 0 0 0 0 0 0 1 0 0
0 0 0 0 0 0 0 1 1 0 0
0 0 0 0 0 0 0 0 1 0 0
0 0 0 0 0 0 0 1 1 0 60
0 0 0 0 0 0 0 0 1 0 60
0 0 0 0 0 0 0 1 1 0 118
0 0 0 0 0 0 0 0 1 0 118
0 0 0 0 0 0 0 1 1 0 0
0 0 0 0 0 0 0 0 1 0 0
0 0 0 0 0 0 0 1 1 0 0
0 0 0 0 0 0 0 0 1 0 0
0 0 0 0 0 0 0 1 1 0 0
0 0 0 0 0 0 0 0 1 0 0
0 0 0 0 0 0 0 1 1 0 0
0 0 0 0 0 0 0 0 1 0 0
0 0 0 0 0 0 0 1 1 0 0
0 0 0 0 0 0 0 0 1 0 0
0 0 0 0 0 0 0 1 1 0 0
0 0 0 0 0 0 0 0 1 0 0
0 0 0 0 0 0 0 1 1 0 0
0 0 0 0 0 0 0 0 1 0 0
0 0 0 0 0 0 0 1 1 0 0
0 0 0 0 0 0 0 0 1 0 0
0 0 0 0 0 0 0 1 1 0 0
0 0 0 0 0 0 0 0 1 0 0
0 0 0 0 0 0 0 1 1 0 0
0 0 0 0 0 0 0 0 1 0 0
0 0 0 0 0 0 0 1 1 0 0
0 0 0 0 0 0 0 0 1 0 0
0 0 0 0 0 0 0 1 1 0 0
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*/

/* Test case 07_P06T1:
M N progIN reset progLoad start result clk valid done output
0 0 0 0 0 0 0 0 x x x
0 0 0 0 0 0 0 1 x x x
0 0 0 1 0 0 0 0 x x x
0 0 0 1 0 0 0 1 0 0 x
0 0 0 0 0 0 0 0 0 0 x
0 0 0 0 0 0 0 1 0 0 x
0 0 0 0 0 0 0 0 0 0 x
0 0 0 0 0 0 0 1 0 0 x
0 0 0 0 0 0 0 0 0 0 x
0 0 0 0 0 0 0 1 0 0 x
0 0 0 0 0 0 0 0 0 0 x
0 0 0 0 0 0 0 1 0 0 x
0 0 0 0 0 0 0 0 0 0 x
0 0 0 0 0 0 0 1 0 0 x
0 0 0 0 0 0 0 0 0 0 x
0 0 0 0 0 0 0 1 0 0 x
0 0 0 0 0 0 0 0 0 0 x
0 0 0 0 0 0 0 1 0 0 x
0 0 0 0 0 0 0 0 0 0 x
0 0 0 0 0 0 0 1 0 0 x
0 0 0 0 0 0 0 0 0 0 x
0 0 0 0 0 0 0 1 0 0 x
0 0 0 0 0 0 0 0 0 0 x
0 0 0 0 0 0 0 1 0 0 x
0 0 0 0 0 0 0 0 0 0 x
0 0 0 0 0 0 0 1 0 0 x
0 0 0 0 0 0 0 0 0 0 x
0 0 0 0 0 0 0 1 0 0 x
0 0 0 0 0 0 0 0 0 0 x
0 0 0 0 0 0 0 1 0 0 x
0 0 0 0 0 0 0 0 0 0 x
0 0 0 0 0 0 0 1 0 0 x
0 0 0 0 0 0 0 0 0 0 x
0 0 0 0 0 0 0 1 0 0 x
0 0 0 0 0 0 0 0 0 0 x
0 0 0 0 0 0 0 1 0 0 x
0 0 0 0 0 0 0 0 0 0 x
0 0 0 0 0 0 0 1 0 0 x
0 0 0 0 0 0 0 0 0 0 x
0 0 0 0 0 0 0 1 0 0 x
0 0 0 0 0 0 0 0 0 0 x
0 0 0 0 0 0 0 1 0 0 x
0 0 1792 0 1 0 0 0 0 0 x
0 0 1792 0 1 0 0 1 0 0 x
0 0 1536 0 1 0 0 0 0 0 x
0 0 1536 0 1 0 0 1 0 0 x
0 0 2817 0 1 0 0 0 0 0 x
0 0 2817 0 1 0 0 1 0 0 x
0 0 2048 0 1 0 0 0 0 0 x
0 0 2048 0 1 0 0 1 0 0 x
0 0 1536 0 1 0 0 0 0 0 x
0 0 1536 0 1 0 0 1 0 0 x
0 0 2818 0 1 0 0 0 0 0 x
0 0 2818 0 1 0 0 1 0 0 x
0 0 1024 0 1 0 0 0 0 0 x
0 0 1024 0 1 0 0 1 0 0 x
0 0 2561 0 1 0 0 0 0 0 x
0 0 2561 0 1 0 0 1 0 0 x
0 0 4864 0 1 0 0 0 0 0 x
0 0 4864 0 1 0 0 1 0 0 x
0 0 2819 0 1 0 0 0 0 0 x
0 0 2819 0 1 0 0 1 0 0 x
0 0 2561 0 1 0 0 0 0 0 x
0 0 2561 0 1 0 0 1 0 0 x
0 0 5120 0 1 0 0 0 0 0 x
0 0 5120 0 1 0 0 1 0 0 x
0 0 2820 0 1 0 0 0 0 0 x
0 0 2820 0 1 0 0 1 0 0 x
0 0 7936 0 1 0 0 0 0 0 x
0 0 7936 0 1 0 0 1 0 0 x
15 7 0 0 0 1 0 0 0 0 x
15 7 0 0 0 1 0 1 0 0 x
15 7 0 0 0 0 0 0 x 0 x
15 7 0 0 0 0 0 1 x 0 x
15 7 0 0 0 0 0 0 x 0 x
15 7 0 0 0 0 0 1 x 0 x
15 7 0 0 0 0 0 0 x 0 x
15 7 0 0 0 0 0 1 x 0 x
15 7 0 0 0 0 0 0 x 0 x
15 7 0 0 0 0 0 1 x 0 x
15 7 0 0 0 0 0 0 x 0 x
15 7 0 0 0 0 0 1 x 0 x
15 7 0 0 0 0 0 0 x 0 x
15 7 0 0 0 0 0 1 x 0 x
15 7 0 0 0 0 0 0 x 0 x
15 7 0 0 0 0 0 1 x 0 x
15 7 0 0 0 0 0 0 x 0 x
15 7 0 0 0 0 0 1 x 0 x
15 7 0 0 0 0 0 0 x 0 x
15 7 0 0 0 0 0 1 x 0 x
15 7 0 0 0 0 0 0 x 0 x
15 7 0 0 0 0 0 1 x 0 x
15 7 0 0 0 0 0 0 x 0 x
15 7 0 0 0 0 0 1 x 0 x
15 7 0 0 0 0 0 0 x 0 x
15 7 0 0 0 0 0 1 x 0 x
15 7 0 0 0 0 0 0 x 0 x
15 7 0 0 0 0 0 1 x 0 x
15 7 0 0 0 0 0 0 x 0 x
15 7 0 0 0 0 0 1 x 0 x
15 7 0 0 0 0 0 0 x 0 x
15 7 0 0 0 0 0 1 x 0 x
15 7 0 0 0 0 0 0 x 0 x
15 7 0 0 0 0 0 1 x 0 x
15 7 0 0 0 0 0 0 x 0 x
15 7 0 0 0 0 0 1 x 0 x
15 7 0 0 0 0 0 0 x 0 x
15 7 0 0 0 0 0 1 x 0 x
15 7 0 0 0 0 0 0 x 0 x
15 7 0 0 0 0 0 1 x 0 x
15 7 0 0 0 0 0 0 x 0 x
0 0 0 0 0 0 0 1 x 0 x
0 0 0 0 0 0 0 0 x 0 x
0 0 0 0 0 0 0 1 x 0 x
0 0 0 0 0 0 0 0 x 0 x
0 0 0 0 0 0 0 1 x 0 x
0 0 0 0 0 0 0 0 x 0 x
0 0 0 0 0 0 0 1 x 0 x
0 0 0 0 0 0 0 0 x 0 x
0 0 0 0 0 0 0 1 x 0 x
0 0 0 0 0 0 0 0 x 0 x
0 0 0 0 0 0 0 1 x 0 x
0 0 0 0 0 0 0 0 x 0 x
0 0 0 0 0 0 0 1 1 0 x
0 0 0 0 0 0 1 0 1 0 0
0 0 0 0 0 0 1 1 1 0 0
0 0 0 0 0 0 0 0 1 0 0
0 0 0 0 0 0 0 1 1 0 15
0 0 0 0 0 0 0 0 1 0 15
0 0 0 0 0 0 0 1 1 0 7
0 0 0 0 0 0 0 0 1 0 7
0 0 0 0 0 0 0 1 1 0 105
0 0 0 0 0 0 0 0 1 0 105
0 0 0 0 0 0 0 1 1 0 2
0 0 0 0 0 0 0 0 1 0 2
0 0 0 0 0 0 0 1 1 0 0
0 0 0 0 0 0 0 0 1 0 0
0 0 0 0 0 0 0 1 1 0 0
0 0 0 0 0 0 0 0 1 0 0
0 0 0 0 0 0 0 1 1 0 0
0 0 0 0 0 0 0 0 1 0 0
0 0 0 0 0 0 0 1 1 0 0
0 0 0 0 0 0 0 0 1 0 0
0 0 0 0 0 0 0 1 1 0 0
0 0 0 0 0 0 0 0 1 0 0
0 0 0 0 0 0 0 1 1 0 0
0 0 0 0 0 0 0 0 1 0 0
0 0 0 0 0 0 0 1 1 0 0
0 0 0 0 0 0 0 0 1 0 0
0 0 0 0 0 0 0 1 1 0 0
0 0 0 0 0 0 0 0 1 0 0
0 0 0 0 0 0 0 1 1 0 0
0 0 0 0 0 0 0 0 1 0 0
0 0 0 0 0 0 0 1 1 0 0
0 0 0 0 0 0 0 0 1 0 0
0 0 0 0 0 0 0 1 1 0 0
0 0 0 0 0 0 0 0 1 0 0
0 0 0 0 0 0 0 1 1 1 x
0 0 0 0 0 0 0 0 1 1 x
0 0 0 0 0 0 0 1 1 1 x
0 0 0 0 0 0 0 0 1 1 x
*/

/* Test case 02_P01T02:
M N progIN reset progLoad start result clk valid done output
0 0 0 0 0 0 0 0 x x x
0 0 0 0 0 0 0 1 x x x
0 0 0 1 0 0 0 0 x x x
0 0 0 1 0 0 0 1 0 0 0
0 0 0 0 0 0 0 0 0 0 0
0 0 0 0 0 0 0 1 0 0 0
0 0 0 0 0 0 0 0 0 0 0
0 0 0 0 0 0 0 1 0 0 0
0 0 0 0 0 0 0 0 0 0 0
0 0 0 0 0 0 0 1 0 0 0
0 0 0 0 0 0 0 0 0 0 0
0 0 0 0 0 0 0 1 0 0 0
0 0 0 0 0 0 0 0 0 0 0
0 0 0 0 0 0 0 1 0 0 0
0 0 0 0 0 0 0 0 0 0 0
0 0 0 0 0 0 0 1 0 0 0
0 0 0 0 0 0 0 0 0 0 0
0 0 0 0 0 0 0 1 0 0 0
0 0 0 0 0 0 0 0 0 0 0
0 0 0 0 0 0 0 1 0 0 0
0 0 0 0 0 0 0 0 0 0 0
0 0 0 0 0 0 0 1 0 0 0
0 0 0 0 0 0 0 0 0 0 0
0 0 0 0 0 0 0 1 0 0 0
0 0 0 0 0 0 0 0 0 0 0
0 0 0 0 0 0 0 1 0 0 0
0 0 0 0 0 0 0 0 0 0 0
0 0 0 0 0 0 0 1 0 0 0
0 0 0 0 0 0 0 0 0 0 0
0 0 0 0 0 0 0 1 0 0 0
0 0 0 0 0 0 0 0 0 0 0
0 0 0 0 0 0 0 1 0 0 0
0 0 0 0 0 0 0 0 0 0 0
0 0 0 0 0 0 0 1 0 0 0
0 0 0 0 0 0 0 0 0 0 0
0 0 0 0 0 0 0 1 0 0 0
0 0 0 0 0 0 0 0 0 0 0
0 0 0 0 0 0 0 1 0 0 0
0 0 0 0 0 0 0 0 0 0 0
0 0 0 0 0 0 0 1 0 0 0
0 0 0 0 0 0 0 0 0 0 0
0 0 0 0 0 0 0 1 0 0 0
0 0 271 0 1 0 0 0 0 0 0
0 0 271 0 1 0 0 1 0 0 0
0 0 565 0 1 0 0 0 0 0 0
0 0 565 0 1 0 0 1 0 0 0
0 0 4352 0 1 0 0 0 0 0 0
0 0 4352 0 1 0 0 1 0 0 0
0 0 2819 0 1 0 0 0 0 0 0
0 0 2819 0 1 0 0 1 0 0 0
0 0 7936 0 1 0 0 0 0 0 0
0 0 7936 0 1 0 0 1 0 0 0
0 0 0 0 0 1 0 0 0 0 0
0 0 0 0 0 1 0 1 0 0 0
0 0 0 0 0 0 0 0 x 0 0
0 0 0 0 0 0 0 1 x 0 0
0 0 0 0 0 0 0 0 x 0 0
0 0 0 0 0 0 0 1 x 0 0
0 0 0 0 0 0 0 0 x 0 0
0 0 0 0 0 0 0 1 x 0 0
0 0 0 0 0 0 0 0 x 0 0
0 0 0 0 0 0 0 1 x 0 0
0 0 0 0 0 0 0 0 x 0 0
0 0 0 0 0 0 0 1 x 0 0
0 0 0 0 0 0 0 0 x 0 0
0 0 0 0 0 0 0 1 x 0 0
0 0 0 0 0 0 0 0 x 0 0
0 0 0 0 0 0 0 1 x 0 0
0 0 0 0 0 0 0 0 x 0 0
0 0 0 0 0 0 0 1 x 0 0
0 0 0 0 0 0 0 0 x 0 0
0 0 0 0 0 0 0 1 x 0 0
0 0 0 0 0 0 0 0 x 0 0
0 0 0 0 0 0 0 1 x 0 0
0 0 0 0 0 0 0 0 x 0 0
0 0 0 0 0 0 0 1 x 0 0
0 0 0 0 0 0 0 0 x 0 0
0 0 0 0 0 0 0 1 x 0 0
0 0 0 0 0 0 0 0 x 0 0
0 0 0 0 0 0 0 1 x 0 0
0 0 0 0 0 0 0 0 x 0 0
0 0 0 0 0 0 0 1 x 0 0
0 0 0 0 0 0 0 0 x 0 0
0 0 0 0 0 0 0 1 x 0 0
0 0 0 0 0 0 0 0 x 0 0
0 0 0 0 0 0 0 1 x 0 0
0 0 0 0 0 0 0 0 x 0 0
0 0 0 0 0 0 0 1 x 0 0
0 0 0 0 0 0 0 0 x 0 0
0 0 0 0 0 0 0 1 x 0 0
0 0 0 0 0 0 0 0 x 0 0
0 0 0 0 0 0 0 1 x 0 0
0 0 0 0 0 0 0 0 x 0 0
0 0 0 0 0 0 0 1 x 0 0
0 0 0 0 0 0 0 0 x 0 0
0 0 0 0 0 0 0 1 x 0 0
0 0 0 0 0 0 0 0 x 0 0
0 0 0 0 0 0 0 1 x 0 0
0 0 0 0 0 0 0 0 x 0 0
0 0 0 0 0 0 0 1 x 0 0
0 0 0 0 0 0 0 0 x 0 0
0 0 0 0 0 0 0 1 x 0 0
0 0 0 0 0 0 0 0 x 0 0
0 0 0 0 0 0 0 1 x 0 0
0 0 0 0 0 0 0 0 x 0 0
0 0 0 0 0 0 0 1 1 0 0
0 0 0 0 0 0 1 0 1 0 0
0 0 0 0 0 0 1 1 1 0 0
0 0 0 0 0 0 0 0 1 0 0
0 0 0 0 0 0 0 1 1 0 0
0 0 0 0 0 0 0 0 1 0 0
0 0 0 0 0 0 0 1 1 0 0
0 0 0 0 0 0 0 0 1 0 0
0 0 0 0 0 0 0 1 1 0 68
0 0 0 0 0 0 0 0 1 0 68
0 0 0 0 0 0 0 1 1 0 0
0 0 0 0 0 0 0 0 1 0 0
0 0 0 0 0 0 0 1 1 0 0
0 0 0 0 0 0 0 0 1 0 0
0 0 0 0 0 0 0 1 1 0 0
0 0 0 0 0 0 0 0 1 0 0
0 0 0 0 0 0 0 1 1 0 0
0 0 0 0 0 0 0 0 1 0 0
0 0 0 0 0 0 0 1 1 0 0
0 0 0 0 0 0 0 0 1 0 0
0 0 0 0 0 0 0 1 1 0 0
0 0 0 0 0 0 0 0 1 0 0
0 0 0 0 0 0 0 1 1 0 0
0 0 0 0 0 0 0 0 1 0 0
0 0 0 0 0 0 0 1 1 0 0
0 0 0 0 0 0 0 0 1 0 0
0 0 0 0 0 0 0 1 1 0 0
0 0 0 0 0 0 0 0 1 0 0
0 0 0 0 0 0 0 1 1 0 0
0 0 0 0 0 0 0 0 1 0 0
0 0 0 0 0 0 0 1 1 0 0
0 0 0 0 0 0 0 0 1 0 0
0 0 0 0 0 0 0 1 1 0 0
0 0 0 0 0 0 0 0 1 0 0
0 0 0 0 0 0 0 1 1 1 0
0 0 0 0 0 0 0 0 1 1 0
0 0 0 0 0 0 0 1 1 1 0
0 0 0 0 0 0 0 0 1 1 0
0 0 0 0 0 0 0 1 1 1 0
0 0 0 0 0 0 1 0 1 X 0
0 0 0 0 0 0 1 1 1 X 0
0 0 0 0 0 0 0 0 1 0 0
0 0 0 0 0 0 0 1 1 0 0
0 0 0 0 0 0 0 0 1 0 0
0 0 0 0 0 0 0 1 1 0 0
0 0 0 0 0 0 0 0 1 0 0
0 0 0 0 0 0 0 1 1 0 68
0 0 0 0 0 0 0 0 1 0 68
0 0 0 0 0 0 0 1 1 0 0
0 0 0 0 0 0 0 0 1 0 0
0 0 0 0 0 0 0 1 1 0 0
0 0 0 0 0 0 0 0 1 0 0
0 0 0 0 0 0 0 1 1 0 0
0 0 0 0 0 0 0 0 1 0 0
0 0 0 0 0 0 0 1 1 0 0
0 0 0 0 0 0 0 0 1 0 0
0 0 0 0 0 0 0 1 1 0 0
0 0 0 0 0 0 0 0 1 0 0
0 0 0 0 0 0 0 1 1 0 0
0 0 0 0 0 0 0 0 1 0 0
0 0 0 0 0 0 0 1 1 0 0
0 0 0 0 0 0 0 0 1 0 0
0 0 0 0 0 0 0 1 1 0 0
0 0 0 0 0 0 0 0 1 0 0
0 0 0 0 0 0 0 1 1 0 0
0 0 0 0 0 0 0 0 1 0 0
0 0 0 0 0 0 0 1 1 0 0
0 0 0 0 0 0 0 0 1 0 0
0 0 0 0 0 0 0 1 1 0 0
0 0 0 0 0 0 0 0 1 0 0
0 0 0 0 0 0 0 1 1 0 0
0 0 0 0 0 0 0 0 1 0 0
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*/

/* Test case 05_P04T1:
M N progIN reset progLoad start result clk valid done output
0 0 0 0 0 0 0 0 x x x
0 0 0 0 0 0 0 1 x x x
0 0 0 1 0 0 0 0 x x x
0 0 0 1 0 0 0 1 0 0 x
0 0 0 0 0 0 0 0 0 0 x
0 0 0 0 0 0 0 1 0 0 x
0 0 0 0 0 0 0 0 0 0 x
0 0 0 0 0 0 0 1 0 0 x
0 0 0 0 0 0 0 0 0 0 x
0 0 0 0 0 0 0 1 0 0 x
0 0 0 0 0 0 0 0 0 0 x
0 0 0 0 0 0 0 1 0 0 x
0 0 0 0 0 0 0 0 0 0 x
0 0 0 0 0 0 0 1 0 0 x
0 0 0 0 0 0 0 0 0 0 x
0 0 0 0 0 0 0 1 0 0 x
0 0 0 0 0 0 0 0 0 0 x
0 0 0 0 0 0 0 1 0 0 x
0 0 0 0 0 0 0 0 0 0 x
0 0 0 0 0 0 0 1 0 0 x
0 0 0 0 0 0 0 0 0 0 x
0 0 0 0 0 0 0 1 0 0 x
0 0 0 0 0 0 0 0 0 0 x
0 0 0 0 0 0 0 1 0 0 x
0 0 0 0 0 0 0 0 0 0 x
0 0 0 0 0 0 0 1 0 0 x
0 0 0 0 0 0 0 0 0 0 x
0 0 0 0 0 0 0 1 0 0 x
0 0 0 0 0 0 0 0 0 0 x
0 0 0 0 0 0 0 1 0 0 x
0 0 0 0 0 0 0 0 0 0 x
0 0 0 0 0 0 0 1 0 0 x
0 0 0 0 0 0 0 0 0 0 x
0 0 0 0 0 0 0 1 0 0 x
0 0 0 0 0 0 0 0 0 0 x
0 0 0 0 0 0 0 1 0 0 x
0 0 0 0 0 0 0 0 0 0 x
0 0 0 0 0 0 0 1 0 0 x
0 0 0 0 0 0 0 0 0 0 x
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*/

/* Test case 08_P06T2:
M N progIN reset progLoad start result clk valid done output
0 0 0 0 0 0 0 0 x x x
0 0 0 0 0 0 0 1 x x x
0 0 0 1 0 0 0 0 x x x
0 0 0 1 0 0 0 1 0 0 x
0 0 0 0 0 0 0 0 0 0 x
0 0 0 0 0 0 0 1 0 0 x
0 0 0 0 0 0 0 0 0 0 x
0 0 0 0 0 0 0 1 0 0 x
0 0 0 0 0 0 0 0 0 0 x
0 0 0 0 0 0 0 1 0 0 x
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*/

/* Test case 03_P02T01:
M N progIN reset progLoad start result clk valid done output
0 0 0 0 0 0 0 0 x x x
0 0 0 0 0 0 0 1 x x x
0 0 0 1 0 0 0 0 x x x
0 0 0 1 0 0 0 1 0 0 0
0 0 0 0 0 0 0 0 0 0 0
0 0 0 0 0 0 0 1 0 0 0
0 0 0 0 0 0 0 0 0 0 0
0 0 0 0 0 0 0 1 0 0 0
0 0 0 0 0 0 0 0 0 0 0
0 0 0 0 0 0 0 1 0 0 0
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*/

/* Test case 06_P05T1:
M N progIN reset progLoad start result clk valid done output
0 0 0 0 0 0 0 0 x x x
0 0 0 0 0 0 0 1 x x x
0 0 0 1 0 0 0 0 x x x
0 0 0 1 0 0 0 1 0 0 x
0 0 0 0 0 0 0 0 0 0 x
0 0 0 0 0 0 0 1 0 0 x
0 0 0 0 0 0 0 0 0 0 x
0 0 0 0 0 0 0 1 0 0 x
0 0 0 0 0 0 0 0 0 0 x
0 0 0 0 0 0 0 1 0 0 x
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*/
