// Digital circuit TEMPLATE Vnew.dig as structural Verilog
module TEMPLATE_Vnew (
  input  [7:0] M,
  input  [7:0] N,
  input  [12:0] progIN,
  input  reset,
  input  progLoad,
  input  start,
  input  result,
  input  clk,
  input  in_13,
  input  in_14,
  input  data,
  output valid,
  output done,
  output [7:0] \output ,
  output [7:0] Z,
  output [1:0] out_15,
  output [12:0] out_17,
  output [4:0] out_18
);

  wire and_1_out, and_2_out, t_ff_1_q;
  wire [7:0] add_1_s, counter_1_out, multiplexer_1_out;
  wire [12:0] dIn;

  LED led_1 (.in(result));
  and and_1 (and_1_out, start, ~t_ff_1_q);  // And
  and and_2 (and_2_out, clk, progLoad);
  Multiplexer #(.Bits(8), .Selector_Bits(2)) multiplexer_1 (
    .sel({in_14, in_13}), .in_0(add_1_s), .in_1(8'h1), .in_2({8{1'b0}}), .in_3({8{1'b0}}),
    .out(multiplexer_1_out));
  T_FF t_ff_1 (.T(and_1_out), .C(clk), .Q(t_ff_1_q));  // open: nQ
  Counter #(.Bits(8)) counter_1 (.en(progLoad), .C(and_2_out), .clr(reset), .out(counter_1_out));  // open: ovf
  BlockRAMDualPort #(.AddrBits(1), .Bits(8)) blockramdualport_1 (
    .A(1'b0), .Din(multiplexer_1_out), .str(t_ff_1_q), .C(clk), .D(Z));
  Add #(.Bits(8)) add_1 (.a(Z), .b(8'h1), .c_i(1'b0), .s(add_1_s));  // open: c_o
  D_FF #(.Bits(13)) d_ff_1 (.D(progIN), .C(~clk), .Q(dIn));  // open: nQ
  RAMDualAccess #(.AddrBits(8), .Bits(13)) pRAM (
    .str(progLoad), .C(clk), .ld(1'b0), .A1(counter_1_out), .Din1(dIn), .A2(Z), .D2(out_17));  // open: D1
  Register accA (.D(data), .C(clk), .en(1'b0));  // open: Q
  Register accB (.D(data), .C(clk), .en(1'b0));  // open: Q
  Register regC (.D(data), .C(clk), .en(1'b0));  // open: Q
  Seven_Seg_Hex seven_seg_hex_1 (.d(4'b0000), .dp(1'b0));
  Seven_Seg_Hex seven_seg_hex_2 (.d(4'b0001), .dp(1'b0));

  assign done = 1'b0;
  assign out_15 = {in_14, in_13};
  assign out_18 = out_17[12:8];
  assign \output  = 8'h1;
  assign valid = 1'b0;

  // Other names for the same wires on the sheet: operand[7:0] = out_17[7:0]; opCode[4:0] = out_17[12:8]; pc[7:0] = Z;
  //   pIn[12:0] = progIN; pLoad = progLoad

  // Notes on the sheet:
  //   Control Unit
  //   Jump
  //   Reset
  //   PC
endmodule

/* Test case 01_P01T01:
M N progIN reset progLoad start result clk valid done output
0 0 0 0 0 0 0 0 0 0 0
0 0 0 0 0 0 0 1 0 0 0
0 0 0 1 0 0 0 0 0 0 0
0 0 0 1 0 0 0 1 0 0 0
0 0 0 0 0 0 0 0 0 0 0
0 0 0 0 0 0 0 1 0 0 0
0 0 0 0 0 0 0 0 0 0 0
0 0 0 0 0 0 0 1 0 0 0
0 0 0 0 0 0 0 0 0 0 0
0 0 0 0 0 0 0 1 0 0 0
0 0 0 0 0 0 0 0 0 0 0
0 0 0 0 0 0 0 1 0 0 0
0 0 0 0 0 0 0 0 0 0 0
0 0 0 0 0 0 0 1 0 0 0
0 0 0 0 0 0 0 0 0 0 0
0 0 0 0 0 0 0 1 0 0 0
0 0 0 0 0 0 0 0 0 0 0
0 0 0 0 0 0 0 1 0 0 0
0 0 0 0 0 0 0 0 0 0 0
0 0 0 0 0 0 0 1 0 0 0
0 0 0 0 0 0 0 0 0 0 0
0 0 0 0 0 0 0 1 0 0 0
0 0 0 0 0 0 0 0 0 0 0
0 0 0 0 0 0 0 1 0 0 0
0 0 0 0 0 0 0 0 0 0 0
0 0 0 0 0 0 0 1 0 0 0
0 0 0 0 0 0 0 0 0 0 0
0 0 0 0 0 0 0 1 0 0 0
0 0 0 0 0 0 0 0 0 0 0
0 0 0 0 0 0 0 1 0 0 0
0 0 0 0 0 0 0 0 0 0 0
0 0 0 0 0 0 0 1 0 0 0
0 0 0 0 0 0 0 0 0 0 0
0 0 0 0 0 0 0 1 0 0 0
0 0 0 0 0 0 0 0 0 0 0
0 0 0 0 0 0 0 1 0 0 0
0 0 0 0 0 0 0 0 0 0 0
0 0 0 0 0 0 0 1 0 0 0
0 0 0 0 0 0 0 0 0 0 0
0 0 0 0 0 0 0 1 0 0 0
0 0 0 0 0 0 0 0 0 0 0
0 0 0 0 0 0 0 1 0 0 0
0 0 271 0 1 0 0 0 0 0 0
0 0 0 0 1 0 0 1 0 0 0
0 0 565 0 1 0 0 0 0 0 0
0 0 0 0 1 0 0 1 0 0 0
0 0 4352 0 1 0 0 0 0 0 0
0 0 0 0 1 0 0 1 0 0 0
0 0 2819 0 1 0 0 0 0 0 0
0 0 0 0 1 0 0 1 0 0 0
0 0 7936 0 1 0 0 0 0 0 0
0 0 0 0 1 0 0 1 0 0 0
0 0 0 0 0 1 0 0 0 0 0
0 0 0 0 0 1 0 1 0 0 0
0 0 0 0 0 0 0 0 x 0 0
0 0 0 0 0 0 0 1 x 0 0
0 0 0 0 0 0 0 0 x 0 0
0 0 0 0 0 0 0 1 x 0 0
0 0 0 0 0 0 0 0 x 0 0
0 0 0 0 0 0 0 1 x 0 0
0 0 0 0 0 0 0 0 x 0 0
0 0 0 0 0 0 0 1 x 0 0
0 0 0 0 0 0 0 0 x 0 0
0 0 0 0 0 0 0 1 x 0 0
0 0 0 0 0 0 0 0 x 0 0
0 0 0 0 0 0 0 1 x 0 0
0 0 0 0 0 0 0 0 x 0 0
0 0 0 0 0 0 0 1 x 0 0
0 0 0 0 0 0 0 0 x 0 0
0 0 0 0 0 0 0 1 x 0 0
0 0 0 0 0 0 0 0 x 0 0
0 0 0 0 0 0 0 1 x 0 0
0 0 0 0 0 0 0 0 x 0 0
0 0 0 0 0 0 0 1 x 0 0
0 0 0 0 0 0 0 0 x 0 0
0 0 0 0 0 0 0 1 x 0 0
0 0 0 0 0 0 0 0 x 0 0
0 0 0 0 0 0 0 1 x 0 0
0 0 0 0 0 0 0 0 x 0 0
0 0 0 0 0 0 0 1 x 0 0
0 0 0 0 0 0 0 0 x 0 0
0 0 0 0 0 0 0 1 x 0 0
0 0 0 0 0 0 0 0 x 0 0
0 0 0 0 0 0 0 1 x 0 0
0 0 0 0 0 0 0 0 x 0 0
0 0 0 0 0 0 0 1 x 0 0
0 0 0 0 0 0 0 0 x 0 0
0 0 0 0 0 0 0 1 x 0 0
0 0 0 0 0 0 0 0 x 0 0
0 0 0 0 0 0 0 1 x 0 0
0 0 0 0 0 0 0 0 x 0 0
0 0 0 0 0 0 0 1 x 0 0
0 0 0 0 0 0 0 0 x 0 0
0 0 0 0 0 0 0 1 x 0 0
0 0 0 0 0 0 0 0 x 0 0
0 0 0 0 0 0 0 1 x 0 0
0 0 0 0 0 0 0 0 x 0 0
0 0 0 0 0 0 0 1 x 0 0
0 0 0 0 0 0 0 0 x 0 0
0 0 0 0 0 0 0 1 x 0 0
0 0 0 0 0 0 0 0 x 0 0
0 0 0 0 0 0 0 1 x 0 0
0 0 0 0 0 0 0 0 x 0 0
0 0 0 0 0 0 0 1 x 0 0
0 0 0 0 0 0 0 0 x 0 0
0 0 0 0 0 0 0 1 1 0 0
0 0 0 0 0 0 1 0 1 0 0
0 0 0 0 0 0 1 1 1 0 0
0 0 0 0 0 0 0 0 1 0 0
0 0 0 0 0 0 0 1 1 0 0
0 0 0 0 0 0 0 0 1 0 0
0 0 0 0 0 0 0 1 1 0 0
0 0 0 0 0 0 0 0 1 0 0
0 0 0 0 0 0 0 1 1 0 68
0 0 0 0 0 0 0 0 1 0 68
0 0 0 0 0 0 0 1 1 0 0
0 0 0 0 0 0 0 0 1 0 0
0 0 0 0 0 0 0 1 1 0 0
0 0 0 0 0 0 0 0 1 0 0
0 0 0 0 0 0 0 1 1 0 0
0 0 0 0 0 0 0 0 1 0 0
0 0 0 0 0 0 0 1 1 0 0
0 0 0 0 0 0 0 0 1 0 0
0 0 0 0 0 0 0 1 1 0 0
0 0 0 0 0 0 0 0 1 0 0
0 0 0 0 0 0 0 1 1 0 0
0 0 0 0 0 0 0 0 1 0 0
0 0 0 0 0 0 0 1 1 0 0
0 0 0 0 0 0 0 0 1 0 0
0 0 0 0 0 0 0 1 1 0 0
0 0 0 0 0 0 0 0 1 0 0
0 0 0 0 0 0 0 1 1 0 0
0 0 0 0 0 0 0 0 1 0 0
0 0 0 0 0 0 0 1 1 0 0
0 0 0 0 0 0 0 0 1 0 0
0 0 0 0 0 0 0 1 1 0 0
0 0 0 0 0 0 0 0 1 0 0
0 0 0 0 0 0 0 1 1 0 0
0 0 0 0 0 0 0 0 1 0 0
0 0 0 0 0 0 0 1 1 1 0
0 0 0 0 0 0 0 0 1 1 0
0 0 0 0 0 0 0 1 1 1 0
0 0 0 0 0 0 0 0 1 1 0
*/
