// Digital circuit final.dig as structural Verilog
module \final  (
  input  [7:0] M,
  input  [7:0] N,
  input  [12:0] progIN,
  input  reset,
  input  progLoad,
  input  start,
  input  result,
  input  clk,
  input  _1,
  output valid,
  output done,
  output [7:0] \output ,
  output [7:0] Z,
  output [1:0] out_13,
  output [12:0] out_14,
  output [4:0] Instruction,
  output [7:0] Z_2
);

  wire _10111eq, _10111gt, _10111ls, _11101eq, accAen, accBen, accCen, and_1_out, and_2_out, and_3_out,
       and_4_out, and_6_out, and_7_out, and_8_out, and_9_out, and_10_out, and_11_out, comparator_1_lt,
       comparator_2_lt, condition, demultiplexer_1_out_1, demultiplexer_1_out_2, demultiplexer_1_out_4,
       demultiplexer_2_out_0, eq, Jump_Op_d, nand_1_out, nand_2_out, nand_3_out, not_1_out, or_1_out,
       or_3_out, or_4_out, or_5_out, or_7_out, or_8_out, or_9_out, ready, reset_Out, result_Out, rRamen,
       t_ff_1_q, undriven;
  wire [0:0] or_6_out;
  wire [1:0] en;
  wire [3:1] eq_gt_ls;
  wire [7:0] _17, _18, _19, _20, _21, _22, _24, _25, _26, _27, _28, accAout, accBout, add_2_s, current, data,
       memory, most_count, multiplexer_2_out, multiplexer_4_out, multiplexer_5_out, multiplexer_11_out,
       multiplexer_12_out, pCount, pDel, rCount, rDel, regCout;
  wire [12:0] dIn, multiplexer_6_out, multiplexer_7_out, pRAM_d2;

  Multiplexer #(.Bits(8)) multiplexer_1 (
    .sel(comparator_1_lt), .in_0(pCount), .in_1({rCount[7:5], done, rCount[3:0]}), .out(most_count));
  Comparator #(.Bits(8)) comparator_1 (
    .a(pCount), .b({rCount[7:5], done, rCount[3:0]}), .lt(comparator_1_lt));  // open: gt, eq
  Multiplexer #(.Bits(8), .Selector_Bits(4)) multiplexer_2 (
    .in_0(out_14[7:0]), .in_1(out_14[7:0]), .in_3(out_14[7:0]), .in_6(out_14[7:0]), .in_7(out_14[7:0]),
    .in_9(out_14[7:0]), .in_11(out_14[7:0]), .out(multiplexer_2_out));  // open: sel, in_2, in_4, in_5, in_8, in_10, in_12, in_13, in_14, in_15
  Multiplexer #(.Bits(8)) multiplexer_3 (.sel(comparator_2_lt), .in_0(pDel), .in_1(rDel), .out(current));
  Comparator #(.Bits(8)) comparator_2 (.a(pDel), .b(rDel), .lt(comparator_2_lt));  // open: gt, eq
  Comparator #(.Bits(8)) address_cmp (.a(current), .b(most_count), .gt(ready));  // open: eq, lt
  and and_1 (and_1_out, ~reset, start, ~t_ff_1_q);  // And
  and and_2 (and_2_out, reset, t_ff_1_q);
  Add #(.Bits(8)) add_1 (.a(accAout), .b(accBout), .c_i(1'b0), .s(_17));  // open: c_o
  Sub #(.Bits(8)) sub_1 (.a(accAout), .b(accBout), .c_i(1'b0), .s(_18));  // open: c_o
  Mul #(.Bits(4)) mul_1 (.a(accAout[3:0]), .b(accBout[3:0]), .mul(_19));
  Div #(.Bits(8)) div_1 (.a(accAout), .b(accBout), .q(_20));  // open: r
  Multiplexer #(.Selector_Bits(2), .Bits(8)) multiplexer_4 (
    .sel({reset, out_13[0]}), .in_0(add_2_s), .in_1(multiplexer_2_out), .in_2({8{1'b0}}), .in_3({8{1'b0}}),
    .out(multiplexer_4_out));
  nand nand_1 (nand_1_out, ~and_1_out, ~and_2_out);  // NAnd
  and and_3 (and_3_out, clk, progLoad);
  T_FF t_ff_1 (.T(nand_1_out), .C(clk), .Q(t_ff_1_q));  // open: nQ
  Counter #(.Bits(8)) counter_1 (.en(progLoad), .C(and_3_out), .clr(reset), .out(pCount));  // open: ovf
  Counter #(.Bits(8)) counter_2 (.en(reset_Out), .C(clk), .clr(ready), .out(pDel));  // open: ovf
  and and_4 (and_4_out, ~valid, clk, t_ff_1_q);  // And
  Multiplexer #(.Bits(8)) multiplexer_5 (.sel(reset_Out), .in_0(pCount), .in_1(pDel), .out(multiplexer_5_out));
  not not_1 (not_1_out, clk);
  D_FF #(.Bits(8)) pc (.D(multiplexer_4_out), .C(and_4_out), .Q(Z));  // open: nQ
  Multiplexer #(.Bits(13)) multiplexer_6 (.sel(reset_Out), .in_0(dIn), .in_1({13{1'b0}}), .out(multiplexer_6_out));
  Div #(.Bits(8)) div_2 (.a(accAout), .b(accBout), .r(_21));  // open: q
  Comparator #(.Bits(8)) comparator_3 (.a(accAout), .b(accBout), .gt(_10111gt), .eq(_10111eq), .lt(_10111ls));
  assign _24 = ~accAout;  // Not not_2, 8 bits wide
  Register #(.Bits(8)) cache (.D(data), .C(not_1_out), .en(1'b1), .Q(Z_2));
  or or_1 (or_1_out, progLoad, reset_Out);
  Add #(.Bits(8)) add_2 (.a(Z), .b(8'h1), .c_i(1'b0), .s(add_2_s));  // open: c_o
  D_FF #(.Bits(13)) d_ff_1 (.D(progIN), .C(~clk), .Q(dIn));  // open: nQ
  RAMDualAccess #(.AddrBits(8), .Bits(13)) pRAM (
    .str(or_1_out), .C(clk), .ld(1'b0), .A1(multiplexer_5_out), .Din1(multiplexer_6_out), .A2(Z), .D2(pRAM_d2));  // open: D1
  ROM #(.AddrBits(6), .Bits(8)) rom_1 (.A({accBout[2:0], accAout[2:0]}), .sel(1'b1), .D(_22));
  Multiplexer #(.Bits(13)) multiplexer_7 (.sel(reset), .in_0(pRAM_d2), .in_1({13{1'b0}}), .out(multiplexer_7_out));
  Multiplexer multiplexer_8 (.sel(undriven), .in_0(multiplexer_7_out[0]), .in_1(1'b0), .out(out_14[0]));
  assign _26 = accAout | accBout;  // Or or_2, 8 bits wide
  assign _25 = accAout & accBout;  // And and_5, 8 bits wide
  assign _27 = accAout ^ accBout;  // XOr xor_1, 8 bits wide
  BarrelShifter #(.Bits(8)) barrelshifter_1 (.in(accAout), .shift({1'b0, accBout[2:0]}), .out(_28));
  or or_3 (or_3_out, reset, accAen);
  or or_4 (or_4_out, reset, accBen);
  or or_5 (or_5_out, reset, accCen);
  Multiplexer #(.Selector_Bits(5), .Bits(8)) multiplexer_9 (
    .sel(Instruction), .in_0({8{1'b0}}), .in_1(out_14[7:0]), .in_2(out_14[7:0]), .in_3(accBout),
    .in_4(accAout), .in_5(accAout), .in_6(regCout), .in_7(M), .in_8(N), .in_9(out_14[7:0]), .in_10(memory),
    .in_11(accAout), .in_12(out_14[7:0]), .in_13(out_14[7:0]), .in_14(out_14[7:0]), .in_15(out_14[7:0]),
    .in_16(out_14[7:0]), .in_17(_17), .in_18(_18), .in_19(_19), .in_20(_20), .in_21(_21), .in_22(_22),
    .in_23(8'h5), .in_24(_24), .in_25(_25), .in_26(_26), .in_27(_27), .in_28(_28), .in_29(8'h5),
    .in_30({8{1'b0}}), .in_31({8{1'b0}}), .out(data));
  Register #(.Bits(8)) accA (.D(data), .C(clk), .en(or_3_out), .Q(accAout));
  Register #(.Bits(8)) accB (.D(data), .C(clk), .en(or_4_out), .Q(accBout));
  Register #(.Bits(8)) regC (.D(data), .C(clk), .en(or_5_out), .Q(regCout));
  ROM #(.AddrBits(8)) rom_2 (.A(accAout), .sel(1'b1), .D(_11101eq));
  or or_6 (or_6_out[0], _11101eq, _10111eq);
  Demultiplexer #(.Selector_Bits(3)) demultiplexer_1 (
    .sel({_10111ls, _10111gt, or_6_out[0]}), .in(1'b1), .out_1(demultiplexer_1_out_1),
    .out_2(demultiplexer_1_out_2), .out_4(demultiplexer_1_out_4));  // open: out_0, out_3, out_5, out_6, out_7
  D_FF equal_flag (.D(demultiplexer_1_out_1), .C(clk), .Q(eq));  // open: nQ
  D_FF greater_flag (.D(demultiplexer_1_out_2), .C(clk), .Q(eq_gt_ls[1]));  // open: nQ
  D_FF lesser_flag (.D(demultiplexer_1_out_4), .C(clk), .Q(eq_gt_ls[2]));  // open: nQ
  and and_6 (and_6_out, ~ready, reset, ~reset_Out);  // And
  and and_7 (and_7_out, ready, reset_Out);
  and and_8 (and_8_out, ~reset, result, ~result_Out);  // And
  and and_9 (and_9_out, reset, result_Out);
  and and_10 (and_10_out, result_Out, ~done, valid);  // And
  or or_7 (or_7_out, start, result);
  nand nand_2 (nand_2_out, ~and_6_out, ~and_7_out);  // NAnd
  nand nand_3 (nand_3_out, ~and_8_out, ~and_9_out);  // NAnd
  Counter #(.Bits(8)) counter_3 (.en(reset_Out), .C(clk), .clr(ready), .out(rDel));  // open: ovf
  Counter #(.Bits(8)) counter_4 (
    .en(and_10_out), .C(clk), .clr(or_7_out), .out({rCount[7:5], done, rCount[3:0]}));  // open: ovf
  Multiplexer #(.Selector_Bits(5), .Bits(2)) multiplexer_10 (
    .sel(Instruction), .in_0(2'b00), .in_1(2'b01), .in_2(2'b10), .in_3(2'b01), .in_4(2'b10), .in_5(2'b11),
    .in_6(2'b01), .in_7(2'b11), .in_8(2'b11), .in_9(2'b01), .in_10(2'b01), .in_11(2'b00), .in_12(2'b00),
    .in_13(2'b00), .in_14(2'b00), .in_15(2'b00), .in_16(2'b00), .in_17(2'b01), .in_18(2'b01), .in_19(2'b01),
    .in_20(2'b01), .in_21(2'b01), .in_22(2'b01), .in_23(2'b00), .in_24(2'b01), .in_25(2'b01), .in_26(2'b01),
    .in_27(2'b01), .in_28(2'b01), .in_29(2'b00), .in_30(2'b00), .in_31(2'b00), .out(en));
  or or_8 (or_8_out, eq, eq_gt_ls[1]);
  and and_11 (and_11_out, Instruction[0], Instruction[1], ~Instruction[2], Instruction[3], ~Instruction[4]);  // And
  T_FF t_ff_2 (.T(nand_2_out), .C(clk), .Q(reset_Out));  // open: nQ
  T_FF t_ff_3 (.T(nand_3_out), .C(clk), .Q(result_Out));  // open: nQ
  Multiplexer #(.Bits(8)) multiplexer_11 (.sel(reset_Out), .in_0(out_14[7:0]), .in_1(rDel), .out(multiplexer_11_out));
  and and_12 (rRamen, and_11_out, demultiplexer_2_out_0);
  Demultiplexer #(.Selector_Bits(2)) demultiplexer_2 (
    .sel(en), .in(_1), .out_0(demultiplexer_2_out_0), .out_1(accAen), .out_2(accBen), .out_3(accCen));
  or or_9 (or_9_out, rRamen, reset_Out);
  Multiplexer #(.Bits(8)) multiplexer_12 (.sel(reset_Out), .in_0(data), .in_1({8{1'b0}}), .out(multiplexer_12_out));
  Multiplexer #(.Selector_Bits(5)) multiplexer_13 (
    .sel(Instruction), .in_0(1'b1), .in_1(1'b0), .in_2(1'b0), .in_3(1'b0), .in_4(1'b0), .in_5(1'b0),
    .in_6(1'b0), .in_7(1'b0), .in_8(1'b0), .in_9(1'b0), .in_10(1'b0), .in_11(1'b0), .in_12(1'b1), .in_13(eq),
    .in_14(eq_gt_ls[1]), .in_15(eq_gt_ls[2]), .in_16(or_8_out), .in_17(1'b0), .in_18(1'b0), .in_19(1'b0),
    .in_20(1'b0), .in_21(1'b0), .in_22(1'b0), .in_23(1'b0), .in_24(1'b0), .in_25(1'b0), .in_26(1'b0),
    .in_27(1'b0), .in_28(1'b0), .in_29(1'b0), .in_30(1'b0), .in_31(1'b0), .out(condition));
  RAMDualAccess #(.AddrBits(8), .Bits(8)) rRAM (
    .str(or_9_out), .C(clk), .ld(1'b1), .A1(multiplexer_11_out), .Din1(multiplexer_12_out),
    .A2({rCount[7:5], done, rCount[3:0]}), .D1(memory), .D2(\output ));
  ROM #(.AddrBits(5)) Jump_Op (.A(Instruction), .sel(1'b1), .D(Jump_Op_d));
  and and_13 (valid, Instruction[0], Instruction[1], Instruction[2], Instruction[3], Instruction[4]);
  and and_14 (out_13[0], condition, Jump_Op_d);
  and and_15 (eq_gt_ls[3], ~Instruction[0], ~Instruction[1], ~Instruction[2], ~Instruction[3], Instruction[4]);  // And
  Seven_Seg_Hex seven_seg_hex_1 (.d(\output [7:4]), .dp(1'b0));
  Seven_Seg_Hex seven_seg_hex_2 (.d(\output [3:0]), .dp(1'b0));
  // Pins of 1 and 13 bits meet at {Instruction, out_14[7:0]}
  // Pins of 1 and 13 bits meet at multiplexer_7_out
  // Pins of 1 and 13 bits meet at {13{1'b0}}

  assign out_13[1] = reset;
  assign out_14[12:8] = Instruction;

  // Other names for the same wires on the sheet: eq_gt_ls[0] = eq; gt = eq_gt_ls[1]; halt = valid; jump = out_13[0];
  //   ls = eq_gt_ls[2]; operand[7:0] = out_14[7:0]; opCode[4:0] = Instruction; pc[7:0] = Z; pIn[12:0] = progIN;
  //   pLoad = progLoad; rCount[4] = done; st = done; result_In = result

  // Notes on the sheet:
  //   _1: default 1
  //   Input
  //   jump
  //   Reset State
  //   Control Unit
  //   10001
  //   10010
  //   10011
  //   10100
  //   JUMPPPPPPP
  //   Jump
  //   10110
  //   10101
  //   10111
  //   11000
  //   Cache
  //   contents of rom_1 (hex, n*v repeats v):
  //   0,7*1,0,1,2,3,4,5,6,7,0,1,4,9,10,19,24,31,0,1,8,1b,40,7d,d8,157
  //   ,0,1,10,51,100,41,510,961,0,1,20,f3,400,c35,1e60,41a7,0,1,40,2d9
  //   ,1000,3d09,b640,44f1,0,1,80,88b,4000,1312d,44580,c90f7
  //   out idel minnie
  //   11001
  //   11010
  //   11011
  //   11100
  //   Register
  //   Alu
  //   11101
  //   flag
  //   contents of rom_2 (hex, n*v repeats v):
  //   0,0,1,1,0,1,0,1,0,0,0,1,0,1,0,0,0,1,0,1,0,0,0,1,5*0,1,0,1,5*0
  //   ,1,0,0,0,1,0,1,0,0,0,1,5*0,1,5*0,1,0,1,5*0,1,0,0,0,1,0,1,5*0,1
  //   ,0,0,0,1,5*0,1,7*0,1,0,0,0,1,0,1,0,0,0,1,0,1,0,0,0,1,13*0,1,0,0,0
  //   ,1,5*0,1,0,1,9*0,1,0,1,5*0,1,5*0,1,0,0,0,1,5*0,1,5*0,1,0,1,0,1
  //   ,0,0,0,1,0,1,21*0,1,11*0,1,0,0,0,1,0,1,0,0,0,1,5*0,1,0,1,9*0,1
  //   Memory
  //   enWReg 00001-01011
  //   wannajump?
  //   contents of Jump_Op (hex, n*v repeats v):
  //   12*0,5*1
endmodule

/* Test case 01_P01T01:
M N progIN reset progLoad start result clk valid done output
0 0 0 0 0 0 0 0 0 0 0
0 0 0 0 0 0 0 1 0 0 0
0 0 0 1 0 0 0 0 0 0 0
0 0 0 1 0 0 0 1 0 0 0
0 0 0 0 0 0 0 0 0 0 0
0 0 0 0 0 0 0 1 0 0 0
0 0 0 0 0 0 0 0 0 0 0
0 0 0 0 0 0 0 1 0 0 0
0 0 0 0 0 0 0 0 0 0 0
0 0 0 0 0 0 0 1 0 0 0
0 0 0 0 0 0 0 0 0 0 0
0 0 0 0 0 0 0 1 0 0 0
0 0 0 0 0 0 0 0 0 0 0
0 0 0 0 0 0 0 1 0 0 0
0 0 0 0 0 0 0 0 0 0 0
0 0 0 0 0 0 0 1 0 0 0
0 0 0 0 0 0 0 0 0 0 0
0 0 0 0 0 0 0 1 0 0 0
0 0 0 0 0 0 0 0 0 0 0
0 0 0 0 0 0 0 1 0 0 0
0 0 0 0 0 0 0 0 0 0 0
0 0 0 0 0 0 0 1 0 0 0
0 0 0 0 0 0 0 0 0 0 0
0 0 0 0 0 0 0 1 0 0 0
0 0 0 0 0 0 0 0 0 0 0
0 0 0 0 0 0 0 1 0 0 0
0 0 0 0 0 0 0 0 0 0 0
0 0 0 0 0 0 0 1 0 0 0
0 0 0 0 0 0 0 0 0 0 0
0 0 0 0 0 0 0 1 0 0 0
0 0 0 0 0 0 0 0 0 0 0
0 0 0 0 0 0 0 1 0 0 0
0 0 0 0 0 0 0 0 0 0 0
0 0 0 0 0 0 0 1 0 0 0
0 0 0 0 0 0 0 0 0 0 0
0 0 0 0 0 0 0 1 0 0 0
0 0 0 0 0 0 0 0 0 0 0
0 0 0 0 0 0 0 1 0 0 0
0 0 0 0 0 0 0 0 0 0 0
0 0 0 0 0 0 0 1 0 0 0
0 0 0 0 0 0 0 0 0 0 0
0 0 0 0 0 0 0 1 0 0 0
0 0 271 0 1 0 0 0 0 0 0
0 0 0 0 1 0 0 1 0 0 0
0 0 565 0 1 0 0 0 0 0 0
0 0 0 0 1 0 0 1 0 0 0
0 0 4352 0 1 0 0 0 0 0 0
0 0 0 0 1 0 0 1 0 0 0
0 0 2819 0 1 0 0 0 0 0 0
0 0 0 0 1 0 0 1 0 0 0
0 0 7936 0 1 0 0 0 0 0 0
0 0 0 0 1 0 0 1 0 0 0
0 0 0 0 0 1 0 0 0 0 0
0 0 0 0 0 1 0 1 0 0 0
0 0 0 0 0 0 0 0 x 0 0
0 0 0 0 0 0 0 1 x 0 0
0 0 0 0 0 0 0 0 x 0 0
0 0 0 0 0 0 0 1 x 0 0
0 0 0 0 0 0 0 0 x 0 0
0 0 0 0 0 0 0 1 x 0 0
0 0 0 0 0 0 0 0 x 0 0
0 0 0 0 0 0 0 1 x 0 0
0 0 0 0 0 0 0 0 x 0 0
0 0 0 0 0 0 0 1 x 0 0
0 0 0 0 0 0 0 0 x 0 0
0 0 0 0 0 0 0 1 x 0 0
0 0 0 0 0 0 0 0 x 0 0
0 0 0 0 0 0 0 1 x 0 0
0 0 0 0 0 0 0 0 x 0 0
0 0 0 0 0 0 0 1 x 0 0
0 0 0 0 0 0 0 0 x 0 0
0 0 0 0 0 0 0 1 x 0 0
0 0 0 0 0 0 0 0 x 0 0
0 0 0 0 0 0 0 1 x 0 0
0 0 0 0 0 0 0 0 x 0 0
0 0 0 0 0 0 0 1 x 0 0
0 0 0 0 0 0 0 0 x 0 0
0 0 0 0 0 0 0 1 x 0 0
0 0 0 0 0 0 0 0 x 0 0
0 0 0 0 0 0 0 1 x 0 0
0 0 0 0 0 0 0 0 x 0 0
0 0 0 0 0 0 0 1 x 0 0
0 0 0 0 0 0 0 0 x 0 0
0 0 0 0 0 0 0 1 x 0 0
0 0 0 0 0 0 0 0 x 0 0
0 0 0 0 0 0 0 1 x 0 0
0 0 0 0 0 0 0 0 x 0 0
0 0 0 0 0 0 0 1 x 0 0
0 0 0 0 0 0 0 0 x 0 0
0 0 0 0 0 0 0 1 x 0 0
0 0 0 0 0 0 0 0 x 0 0
0 0 0 0 0 0 0 1 x 0 0
0 0 0 0 0 0 0 0 x 0 0
0 0 0 0 0 0 0 1 x 0 0
0 0 0 0 0 0 0 0 x 0 0
0 0 0 0 0 0 0 1 x 0 0
0 0 0 0 0 0 0 0 x 0 0
0 0 0 0 0 0 0 1 x 0 0
0 0 0 0 0 0 0 0 x 0 0
0 0 0 0 0 0 0 1 x 0 0
0 0 0 0 0 0 0 0 x 0 0
0 0 0 0 0 0 0 1 x 0 0
0 0 0 0 0 0 0 0 x 0 0
0 0 0 0 0 0 0 1 x 0 0
0 0 0 0 0 0 0 0 x 0 0
0 0 0 0 0 0 0 1 1 0 0
0 0 0 0 0 0 1 0 1 0 0
0 0 0 0 0 0 1 1 1 0 0
0 0 0 0 0 0 0 0 1 0 0
0 0 0 0 0 0 0 1 1 0 0
0 0 0 0 0 0 0 0 1 0 0
0 0 0 0 0 0 0 1 1 0 0
0 0 0 0 0 0 0 0 1 0 0
0 0 0 0 0 0 0 1 1 0 68
0 0 0 0 0 0 0 0 1 0 68
0 0 0 0 0 0 0 1 1 0 0
0 0 0 0 0 0 0 0 1 0 0
0 0 0 0 0 0 0 1 1 0 0
0 0 0 0 0 0 0 0 1 0 0
0 0 0 0 0 0 0 1 1 0 0
0 0 0 0 0 0 0 0 1 0 0
0 0 0 0 0 0 0 1 1 0 0
0 0 0 0 0 0 0 0 1 0 0
0 0 0 0 0 0 0 1 1 0 0
0 0 0 0 0 0 0 0 1 0 0
0 0 0 0 0 0 0 1 1 0 0
0 0 0 0 0 0 0 0 1 0 0
0 0 0 0 0 0 0 1 1 0 0
0 0 0 0 0 0 0 0 1 0 0
0 0 0 0 0 0 0 1 1 0 0
0 0 0 0 0 0 0 0 1 0 0
0 0 0 0 0 0 0 1 1 0 0
0 0 0 0 0 0 0 0 1 0 0
0 0 0 0 0 0 0 1 1 0 0
0 0 0 0 0 0 0 0 1 0 0
0 0 0 0 0 0 0 1 1 0 0
0 0 0 0 0 0 0 0 1 0 0
0 0 0 0 0 0 0 1 1 0 0
0 0 0 0 0 0 0 0 1 0 0
0 0 0 0 0 0 0 1 1 1 0
0 0 0 0 0 0 0 0 1 1 0
0 0 0 0 0 0 0 1 1 1 0
0 0 0 0 0 0 0 0 1 1 0
*/

/* Test case 02_P01T02:
M N progIN reset progLoad start result clk valid done output
0 0 0 0 0 0 0 0 x x x
0 0 0 0 0 0 0 1 x x x
0 0 0 1 0 0 0 0 x x x
0 0 0 1 0 0 0 1 0 0 0
0 0 0 0 0 0 0 0 0 0 0
0 0 0 0 0 0 0 1 0 0 0
0 0 0 0 0 0 0 0 0 0 0
0 0 0 0 0 0 0 1 0 0 0
0 0 0 0 0 0 0 0 0 0 0
0 0 0 0 0 0 0 1 0 0 0
0 0 0 0 0 0 0 0 0 0 0
0 0 0 0 0 0 0 1 0 0 0
0 0 0 0 0 0 0 0 0 0 0
0 0 0 0 0 0 0 1 0 0 0
0 0 0 0 0 0 0 0 0 0 0
0 0 0 0 0 0 0 1 0 0 0
0 0 0 0 0 0 0 0 0 0 0
0 0 0 0 0 0 0 1 0 0 0
0 0 0 0 0 0 0 0 0 0 0
0 0 0 0 0 0 0 1 0 0 0
0 0 0 0 0 0 0 0 0 0 0
0 0 0 0 0 0 0 1 0 0 0
0 0 0 0 0 0 0 0 0 0 0
0 0 0 0 0 0 0 1 0 0 0
0 0 0 0 0 0 0 0 0 0 0
0 0 0 0 0 0 0 1 0 0 0
0 0 0 0 0 0 0 0 0 0 0
0 0 0 0 0 0 0 1 0 0 0
0 0 0 0 0 0 0 0 0 0 0
0 0 0 0 0 0 0 1 0 0 0
0 0 0 0 0 0 0 0 0 0 0
0 0 0 0 0 0 0 1 0 0 0
0 0 0 0 0 0 0 0 0 0 0
0 0 0 0 0 0 0 1 0 0 0
0 0 0 0 0 0 0 0 0 0 0
0 0 0 0 0 0 0 1 0 0 0
0 0 0 0 0 0 0 0 0 0 0
0 0 0 0 0 0 0 1 0 0 0
0 0 0 0 0 0 0 0 0 0 0
0 0 0 0 0 0 0 1 0 0 0
0 0 0 0 0 0 0 0 0 0 0
0 0 0 0 0 0 0 1 0 0 0
0 0 271 0 1 0 0 0 0 0 0
0 0 271 0 1 0 0 1 0 0 0
0 0 565 0 1 0 0 0 0 0 0
0 0 565 0 1 0 0 1 0 0 0
0 0 4352 0 1 0 0 0 0 0 0
0 0 4352 0 1 0 0 1 0 0 0
0 0 2819 0 1 0 0 0 0 0 0
0 0 2819 0 1 0 0 1 0 0 0
0 0 7936 0 1 0 0 0 0 0 0
0 0 7936 0 1 0 0 1 0 0 0
0 0 0 0 0 1 0 0 0 0 0
0 0 0 0 0 1 0 1 0 0 0
0 0 0 0 0 0 0 0 x 0 0
0 0 0 0 0 0 0 1 x 0 0
0 0 0 0 0 0 0 0 x 0 0
0 0 0 0 0 0 0 1 x 0 0
0 0 0 0 0 0 0 0 x 0 0
0 0 0 0 0 0 0 1 x 0 0
0 0 0 0 0 0 0 0 x 0 0
0 0 0 0 0 0 0 1 x 0 0
0 0 0 0 0 0 0 0 x 0 0
0 0 0 0 0 0 0 1 x 0 0
0 0 0 0 0 0 0 0 x 0 0
0 0 0 0 0 0 0 1 x 0 0
0 0 0 0 0 0 0 0 x 0 0
0 0 0 0 0 0 0 1 x 0 0
0 0 0 0 0 0 0 0 x 0 0
0 0 0 0 0 0 0 1 x 0 0
0 0 0 0 0 0 0 0 x 0 0
0 0 0 0 0 0 0 1 x 0 0
0 0 0 0 0 0 0 0 x 0 0
0 0 0 0 0 0 0 1 x 0 0
0 0 0 0 0 0 0 0 x 0 0
0 0 0 0 0 0 0 1 x 0 0
0 0 0 0 0 0 0 0 x 0 0
0 0 0 0 0 0 0 1 x 0 0
0 0 0 0 0 0 0 0 x 0 0
0 0 0 0 0 0 0 1 x 0 0
0 0 0 0 0 0 0 0 x 0 0
0 0 0 0 0 0 0 1 x 0 0
0 0 0 0 0 0 0 0 x 0 0
0 0 0 0 0 0 0 1 x 0 0
0 0 0 0 0 0 0 0 x 0 0
0 0 0 0 0 0 0 1 x 0 0
0 0 0 0 0 0 0 0 x 0 0
0 0 0 0 0 0 0 1 x 0 0
0 0 0 0 0 0 0 0 x 0 0
0 0 0 0 0 0 0 1 x 0 0
0 0 0 0 0 0 0 0 x 0 0
0 0 0 0 0 0 0 1 x 0 0
0 0 0 0 0 0 0 0 x 0 0
0 0 0 0 0 0 0 1 x 0 0
0 0 0 0 0 0 0 0 x 0 0
0 0 0 0 0 0 0 1 x 0 0
0 0 0 0 0 0 0 0 x 0 0
0 0 0 0 0 0 0 1 x 0 0
0 0 0 0 0 0 0 0 x 0 0
0 0 0 0 0 0 0 1 x 0 0
0 0 0 0 0 0 0 0 x 0 0
0 0 0 0 0 0 0 1 x 0 0
0 0 0 0 0 0 0 0 x 0 0
0 0 0 0 0 0 0 1 x 0 0
0 0 0 0 0 0 0 0 x 0 0
0 0 0 0 0 0 0 1 1 0 0
0 0 0 0 0 0 1 0 1 0 0
0 0 0 0 0 0 1 1 1 0 0
0 0 0 0 0 0 0 0 1 0 0
0 0 0 0 0 0 0 1 1 0 0
0 0 0 0 0 0 0 0 1 0 0
0 0 0 0 0 0 0 1 1 0 0
0 0 0 0 0 0 0 0 1 0 0
0 0 0 0 0 0 0 1 1 0 68
0 0 0 0 0 0 0 0 1 0 68
0 0 0 0 0 0 0 1 1 0 0
0 0 0 0 0 0 0 0 1 0 0
0 0 0 0 0 0 0 1 1 0 0
0 0 0 0 0 0 0 0 1 0 0
0 0 0 0 0 0 0 1 1 0 0
0 0 0 0 0 0 0 0 1 0 0
0 0 0 0 0 0 0 1 1 0 0
0 0 0 0 0 0 0 0 1 0 0
0 0 0 0 0 0 0 1 1 0 0
0 0 0 0 0 0 0 0 1 0 0
0 0 0 0 0 0 0 1 1 0 0
0 0 0 0 0 0 0 0 1 0 0
0 0 0 0 0 0 0 1 1 0 0
0 0 0 0 0 0 0 0 1 0 0
0 0 0 0 0 0 0 1 1 0 0
0 0 0 0 0 0 0 0 1 0 0
0 0 0 0 0 0 0 1 1 0 0
0 0 0 0 0 0 0 0 1 0 0
0 0 0 0 0 0 0 1 1 0 0
0 0 0 0 0 0 0 0 1 0 0
0 0 0 0 0 0 0 1 1 0 0
0 0 0 0 0 0 0 0 1 0 0
0 0 0 0 0 0 0 1 1 0 0
0 0 0 0 0 0 0 0 1 0 0
0 0 0 0 0 0 0 1 1 1 0
0 0 0 0 0 0 0 0 1 1 0
0 0 0 0 0 0 0 1 1 1 0
0 0 0 0 0 0 0 0 1 1 0
0 0 0 0 0 0 0 1 1 1 0
0 0 0 0 0 0 1 0 1 X 0
0 0 0 0 0 0 1 1 1 X 0
0 0 0 0 0 0 0 0 1 0 0
0 0 0 0 0 0 0 1 1 0 0
0 0 0 0 0 0 0 0 1 0 0
0 0 0 0 0 0 0 1 1 0 0
0 0 0 0 0 0 0 0 1 0 0
0 0 0 0 0 0 0 1 1 0 68
0 0 0 0 0 0 0 0 1 0 68
0 0 0 0 0 0 0 1 1 0 0
0 0 0 0 0 0 0 0 1 0 0
0 0 0 0 0 0 0 1 1 0 0
0 0 0 0 0 0 0 0 1 0 0
0 0 0 0 0 0 0 1 1 0 0
0 0 0 0 0 0 0 0 1 0 0
0 0 0 0 0 0 0 1 1 0 0
0 0 0 0 0 0 0 0 1 0 0
0 0 0 0 0 0 0 1 1 0 0
0 0 0 0 0 0 0 0 1 0 0
0 0 0 0 0 0 0 1 1 0 0
0 0 0 0 0 0 0 0 1 0 0
0 0 0 0 0 0 0 1 1 0 0
0 0 0 0 0 0 0 0 1 0 0
0 0 0 0 0 0 0 1 1 0 0
0 0 0 0 0 0 0 0 1 0 0
0 0 0 0 0 0 0 1 1 0 0
0 0 0 0 0 0 0 0 1 0 0
0 0 0 0 0 0 0 1 1 0 0
0 0 0 0 0 0 0 0 1 0 0
0 0 0 0 0 0 0 1 1 0 0
0 0 0 0 0 0 0 0 1 0 0
0 0 0 0 0 0 0 1 1 0 0
0 0 0 0 0 0 0 0 1 0 0
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*/

/* Test case 03_P02T01:
M N progIN reset progLoad start result clk valid done output
0 0 0 0 0 0 0 0 x x x
0 0 0 0 0 0 0 1 x x x
0 0 0 1 0 0 0 0 x x x
0 0 0 1 0 0 0 1 0 0 0
0 0 0 0 0 0 0 0 0 0 0
0 0 0 0 0 0 0 1 0 0 0
0 0 0 0 0 0 0 0 0 0 0
0 0 0 0 0 0 0 1 0 0 0
0 0 0 0 0 0 0 0 0 0 0
0 0 0 0 0 0 0 1 0 0 0
0 0 0 0 0 0 0 0 0 0 0
0 0 0 0 0 0 0 1 0 0 0
0 0 0 0 0 0 0 0 0 0 0
0 0 0 0 0 0 0 1 0 0 0
0 0 0 0 0 0 0 0 0 0 0
0 0 0 0 0 0 0 1 0 0 0
0 0 0 0 0 0 0 0 0 0 0
0 0 0 0 0 0 0 1 0 0 0
0 0 0 0 0 0 0 0 0 0 0
0 0 0 0 0 0 0 1 0 0 0
0 0 0 0 0 0 0 0 0 0 0
0 0 0 0 0 0 0 1 0 0 0
0 0 0 0 0 0 0 0 0 0 0
0 0 0 0 0 0 0 1 0 0 0
0 0 0 0 0 0 0 0 0 0 0
0 0 0 0 0 0 0 1 0 0 0
0 0 0 0 0 0 0 0 0 0 0
0 0 0 0 0 0 0 1 0 0 0
0 0 0 0 0 0 0 0 0 0 0
0 0 0 0 0 0 0 1 0 0 0
0 0 0 0 0 0 0 0 0 0 0
0 0 0 0 0 0 0 1 0 0 0
0 0 0 0 0 0 0 0 0 0 0
0 0 0 0 0 0 0 1 0 0 0
0 0 0 0 0 0 0 0 0 0 0
0 0 0 0 0 0 0 1 0 0 0
0 0 0 0 0 0 0 0 0 0 0
0 0 0 0 0 0 0 1 0 0 0
0 0 0 0 0 0 0 0 0 0 0
0 0 0 0 0 0 0 1 0 0 0
0 0 0 0 0 0 0 0 0 0 0
0 0 0 0 0 0 0 1 0 0 0
0 0 271 0 1 0 0 0 0 0 0
0 0 271 0 1 0 0 1 0 0 0
0 0 566 0 1 0 0 0 0 0 0
0 0 566 0 1 0 0 1 0 0 0
0 0 5888 0 1 0 0 0 0 0 0
0 0 5888 0 1 0 0 1 0 0 0
0 0 3599 0 1 0 0 0 0 0 0
0 0 3599 0 1 0 0 1 0 0 0
0 0 4110 0 1 0 0 0 0 0 0
0 0 4110 0 1 0 0 1 0 0 0
0 0 3856 0 1 0 0 0 0 0 0
0 0 3856 0 1 0 0 1 0 0 0
0 0 0 0 1 0 0 0 0 0 0
0 0 0 0 1 0 0 1 0 0 0
0 0 0 0 1 0 0 0 0 0 0
0 0 0 0 1 0 0 1 0 0 0
0 0 0 0 1 0 0 0 0 0 0
0 0 0 0 1 0 0 1 0 0 0
0 0 0 0 1 0 0 0 0 0 0
0 0 0 0 1 0 0 1 0 0 0
0 0 0 0 1 0 0 0 0 0 0
0 0 0 0 1 0 0 1 0 0 0
0 0 0 0 1 0 0 0 0 0 0
0 0 0 0 1 0 0 1 0 0 0
0 0 0 0 1 0 0 0 0 0 0
0 0 0 0 1 0 0 1 0 0 0
0 0 0 0 1 0 0 0 0 0 0
0 0 0 0 1 0 0 1 0 0 0
0 0 0 0 1 0 0 0 0 0 0
0 0 0 0 1 0 0 1 0 0 0
0 0 0 0 1 0 0 0 0 0 0
0 0 0 0 1 0 0 1 0 0 0
0 0 4352 0 1 0 0 0 0 0 0
0 0 4352 0 1 0 0 1 0 0 0
0 0 2819 0 1 0 0 0 0 0 0
0 0 2819 0 1 0 0 1 0 0 0
0 0 7936 0 1 0 0 0 0 0 0
0 0 7936 0 1 0 0 1 0 0 0
0 0 0 0 1 0 0 0 0 0 0
0 0 0 0 1 0 0 1 0 0 0
0 0 0 0 0 0 0 0 0 0 0
0 0 0 0 0 0 0 1 0 0 0
0 0 0 0 0 0 0 0 0 0 0
0 0 0 0 0 0 0 1 0 0 0
0 0 0 0 0 0 0 0 0 0 0
0 0 0 0 0 0 0 1 0 0 0
0 0 0 0 0 1 0 0 0 0 0
0 0 0 0 0 1 0 1 0 0 0
0 0 0 0 0 0 0 0 x 0 0
0 0 0 0 0 0 0 1 x 0 0
0 0 0 0 0 0 0 0 x 0 0
0 0 0 0 0 0 0 1 x 0 0
0 0 0 0 0 0 0 0 x 0 0
0 0 0 0 0 0 0 1 x 0 0
0 0 0 0 0 0 0 0 x 0 0
0 0 0 0 0 0 0 1 x 0 0
0 0 0 0 0 0 0 0 x 0 0
0 0 0 0 0 0 0 1 x 0 0
0 0 0 0 0 0 0 0 x 0 0
0 0 0 0 0 0 0 1 x 0 0
0 0 0 0 0 0 0 0 x 0 0
0 0 0 0 0 0 0 1 x 0 0
0 0 0 0 0 0 0 0 x 0 0
0 0 0 0 0 0 0 1 x 0 0
0 0 0 0 0 0 0 0 x 0 0
0 0 0 0 0 0 0 1 x 0 0
0 0 0 0 0 0 0 0 x 0 0
0 0 0 0 0 0 0 1 x 0 0
0 0 0 0 0 0 0 0 x 0 0
0 0 0 0 0 0 0 1 x 0 0
0 0 0 0 0 0 0 0 x 0 0
0 0 0 0 0 0 0 1 x 0 0
0 0 0 0 0 0 0 0 x 0 0
0 0 0 0 0 0 0 1 x 0 0
0 0 0 0 0 0 0 0 x 0 0
0 0 0 0 0 0 0 1 x 0 0
0 0 0 0 0 0 0 0 x 0 0
0 0 0 0 0 0 0 1 x 0 0
0 0 0 0 0 0 0 0 x 0 0
0 0 0 0 0 0 0 1 x 0 0
0 0 0 0 0 0 0 0 x 0 0
0 0 0 0 0 0 0 1 x 0 0
0 0 0 0 0 0 0 0 x 0 0
0 0 0 0 0 0 0 1 x 0 0
0 0 0 0 0 0 0 0 x 0 0
0 0 0 0 0 0 0 1 x 0 0
0 0 0 0 0 0 0 0 x 0 0
0 0 0 0 0 0 0 1 x 0 0
0 0 0 0 0 0 0 0 x 0 0
0 0 0 0 0 0 0 1 x 0 0
0 0 0 0 0 0 0 0 x 0 0
0 0 0 0 0 0 0 1 x 0 0
0 0 0 0 0 0 0 0 x 0 0
0 0 0 0 0 0 0 1 x 0 0
0 0 0 0 0 0 0 0 x 0 0
0 0 0 0 0 0 0 1 x 0 0
0 0 0 0 0 0 0 0 x 0 0
0 0 0 0 0 0 0 1 x 0 0
0 0 0 0 0 0 0 0 x 0 0
0 0 0 0 0 0 0 1 1 0 0
0 0 0 0 0 0 1 0 1 0 0
0 0 0 0 0 0 1 1 1 0 0
0 0 0 0 0 0 0 0 1 0 0
0 0 0 0 0 0 0 1 1 0 0
0 0 0 0 0 0 0 0 1 0 0
0 0 0 0 0 0 0 1 1 0 0
0 0 0 0 0 0 0 0 1 0 0
0 0 0 0 0 0 0 1 1 0 69
0 0 0 0 0 0 0 0 1 0 69
0 0 0 0 0 0 0 1 1 0 0
0 0 0 0 0 0 0 0 1 0 0
0 0 0 0 0 0 0 1 1 0 0
0 0 0 0 0 0 0 0 1 0 0
0 0 0 0 0 0 0 1 1 0 0
0 0 0 0 0 0 0 0 1 0 0
0 0 0 0 0 0 0 1 1 0 0
0 0 0 0 0 0 0 0 1 0 0
0 0 0 0 0 0 0 1 1 0 0
0 0 0 0 0 0 0 0 1 0 0
0 0 0 0 0 0 0 1 1 0 0
0 0 0 0 0 0 0 0 1 0 0
0 0 0 0 0 0 0 1 1 0 0
0 0 0 0 0 0 0 0 1 0 0
0 0 0 0 0 0 0 1 1 0 0
0 0 0 0 0 0 0 0 1 0 0
0 0 0 0 0 0 0 1 1 0 0
0 0 0 0 0 0 0 0 1 0 0
0 0 0 0 0 0 0 1 1 0 0
0 0 0 0 0 0 0 0 1 0 0
0 0 0 0 0 0 0 1 1 0 0
0 0 0 0 0 0 0 0 1 0 0
0 0 0 0 0 0 0 1 1 0 0
0 0 0 0 0 0 0 0 1 0 0
0 0 0 0 0 0 0 1 1 1 0
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*/
