// Digital circuit gcd.dig as structural Verilog
module gcd (
  input  [7:0] A,
  input  [7:0] B,
  input  start,
  input  clear,
  input  clk,
  output busy,
  output [7:0] \output 
);

  wire A0, A1, A2, A3, and_1_out, and_2_out, and_3_out, and_4_out, and_5_out, aq, clear_t, eq, loada, loadb,
       multiplexer_1_out, multiplexer_4_out, or_1_out, Qa, Qb;
  wire [7:0] a_t, b_t, multiplexer_2_out, multiplexer_3_out, sub_1_s, sub_2_s;

  and and_1 (and_1_out, ~eq, aq);  // And
  and and_2 (and_2_out, ~aq, ~eq);  // And
  not not_1 (clear_t, clear);
  or or_1 (or_1_out, and_1_out, and_2_out);
  Multiplexer #(.Selector_Bits(2)) multiplexer_1 (
    .sel({Qa, Qb}), .in_0(1'b0), .in_1(or_1_out), .in_2(1'b0), .in_3(1'b0), .out(multiplexer_1_out));
  Sub #(.Bits(8)) sub_1 (.a(a_t), .b(b_t), .c_i(1'b0), .s(sub_1_s));  // open: c_o
  Sub #(.Bits(8)) sub_2 (.a(b_t), .b(a_t), .c_i(1'b0), .s(sub_2_s));  // open: c_o
  Comparator #(.Bits(8)) comparator_1 (.a(a_t), .b(b_t), .gt(aq), .eq(eq));  // open: lt
  Multiplexer #(.Bits(8)) multiplexer_2 (.sel(A3), .in_0(A), .in_1(sub_1_s), .out(multiplexer_2_out));
  Multiplexer #(.Bits(8)) multiplexer_3 (.sel(A2), .in_0(B), .in_1(sub_2_s), .out(multiplexer_3_out));
  and and_3 (and_3_out, clear_t, multiplexer_1_out);
  Decoder #(.Selector_Bits(2)) decoder_1 (.sel({Qa, Qb}), .out_0(A0), .out_1(A1), .out_2(A2), .out_3(A3));
  D_FF d_ff_1 (.D(and_3_out), .C(clk), .Q(Qa));  // open: nQ
  Register #(.Bits(8)) u_a (.D(multiplexer_2_out), .C(clk), .en(loada), .Q(a_t));
  Register #(.Bits(8)) u_b (.D(multiplexer_3_out), .C(clk), .en(loadb), .Q(b_t));
  not not_2 (busy, A0);
  or or_2 (loada, A0, A3);
  or or_3 (loadb, A0, A2);
  Register #(.Bits(8)) out (.D(a_t), .C(clk), .en(A1), .Q(\output ));
  and and_4 (and_4_out, aq, ~eq);  // And
  Multiplexer #(.Selector_Bits(2)) multiplexer_4 (
    .sel({Qa, Qb}), .in_0(start), .in_1(and_4_out), .in_2(1'b1), .in_3(1'b1), .out(multiplexer_4_out));
  and and_5 (and_5_out, clear_t, multiplexer_4_out);
  D_FF d_ff_2 (.D(and_5_out), .C(clk), .Q(Qb));  // open: nQ

  // Other names for the same wires on the sheet: c = clk; loadout = A1; out[7:0] = \output ; s = start; sel_a = A3;
  //   sel_b = A2
endmodule

/* Test case:
A B start clear clk busy output
0xF 0x6 0 0 0 0 0
0xF 0x6 0 0 1 X 0
0xF 0x6 1 0 0 X 0
0xF 0x6 1 0 1 X 0
0xF 0x6 1 0 0 X 0
loop(x,1000)
0xF 0x6 0 0 1 X X
0xF 0x6 0 0 0 X X
end loop
0xF 0x6 0 0 0 0 0x3
*/
