// Digital circuit main.dig as structural Verilog
module main (
  input  progLoad,
  input  [12:0] progIN,
  input  start,
  input  reset,
  input  [7:0] M,
  input  [7:0] N,
  input  clk,
  input  result,
  output [7:0] out_5,
  output [12:0] out_6,
  output [12:0] out_7,
  output [7:0] out_8,
  output [7:0] out_9,
  output [7:0] out_12,
  output [7:0] out_13,
  output [12:0] out_14,
  output out_15,
  output out_16,
  output out_17,
  output valid,
  output done,
  output [7:0] \output 
);

  wire accA_en, accA_en1, accA_en3, accA_en6, accA_en9, accA_en10, accA_en17, accA_en18, accA_en19,
       accA_en28, accA_en1010X, accA_enbitwise, accB_en, accB_en2, accB_en4, and_1_out, and_3_out, and_5_out,
       and_6_out, and_7_out, and_8_out, and_9_out, and_10_out, and_11_out, and_12_out, and_13_out,
       and_14_out, and_15_out, and_16_out, and_17_out, and_18_out, and_19_out, and_21_out, and_22_out,
       and_23_out, and_24_out, and_25_out, and_26_out, and_28_out, and_29_out, and_30_out, and_31_out,
       and_32_out, and_33_out, and_34_out, and_35_out, and_36_out, and_37_out, and_38_out, and_39_out,
       and_40_out, and_41_out, and_42_out, and_43_out, and_44_out, and_45_out, and_46_out, and_47_out,
       and_48_out, and_49_out, and_50_out, and_51_out, and_52_out, and_53_out, and_54_out, and_55_out,
       and_56_out, and_57_out, comparator_1_eq, comparator_2_eq, comparator_3_eq, comparator_4_gt,
       comparator_5_eq, comparator_5_gt, comparator_5_lt, d_ff_5_nq, d_ff_7_nq, d_ff_9_nq, d_ff_11_nq,
       d_ff_13_nq, d_ff_15_nq, d_ff_17_nq, d_ff_18_nq, d_ff_19_nq, d_ff_20_nq, d_ff_21_nq, d_ff_23_nq,
       d_ff_24_nq, d_ff_25_q, d_ff_26_nq, d_ff_28_nq, d_ff_30_nq, d_ff_32_nq, d_ff_34_nq, d_ff_36_nq,
       d_ff_38_nq, d_ff_39_nq, d_ff_40_nq, d_ff_41_nq, d_ff_42_nq, d_ff_43_nq, d_ff_45_nq, d_ff_47_nq,
       d_ff_49_nq, d_ff_51_nq, d_ff_53_nq, d_ff_55_nq, d_ff_56_q, d_ff_57_q, d_ff_58_nq, d_ff_59_nq,
       d_ff_60_nq, d_ff_61_nq, d_ff_63_nq, d_ff_63_q, d_ff_64_nq, d_ff_64_q, d_ff_65_nq, d_ff_66_nq, equal23,
       equal29, isprime_1_p2, jump, multiplexer_5_out, multiplexer_40_out, multiplexer_41_out,
       multiplexer_42_out, next, next0, next1, next2, next3, next4, next5, next6, next7, next8, next9,
       next10, next11, next17, next18, next19, next23, next28, next29, next1010X, next_bitwise, next_jump,
       or_1_out, or_2_out, or_3_out, or_4_out, or_5_out, or_7_out, or_8_out, or_9_out, or_11_out, or_12_out,
       or_13_out, or_16_out, or_18_out, or_22_out, or_24_out, or_26_out, or_27_out, or_28_out, pRAM_isRead,
       regC_en, regC_en5, regC_en7, regC_en8, reset_t, result_t, rRAM_inen, rRAM_isRead, start_q, start_t,
       t_ff_2_q;
  wire [0:0] or_6_out;
  wire [3:0] multiplexer_32_out;
  wire [4:0] opcode;
  wire [7:0] accA_in, accA_in1, accA_in3, accA_in6, accA_in9, accA_in10, accA_in17, accA_in18, accA_in19,
       accA_in28, accA_in1010X, accA_inbitwise, accB_in, accB_in2, accB_in4, add_1_s, add_2_s, and_20_out,
       barrelshifter_1_out, d_ff_2_q, d_ff_3_q, d_ff_4_q, d_ff_6_q, d_ff_8_q, d_ff_10_q, d_ff_12_q,
       d_ff_14_q, d_ff_16_q, d_ff_22_q, d_ff_29_q, d_ff_31_q, d_ff_33_q, d_ff_35_q, d_ff_37_q, d_ff_44_q,
       d_ff_46_q, d_ff_48_q, d_ff_50_q, d_ff_52_q, d_ff_54_q, div_1_q, div_1_r, jump_ptr, mul_1_mul,
       multiplexer_2_out, multiplexer_3_out, multiplexer_6_out, multiplexer_7_out, multiplexer_17_out,
       multiplexer_18_out, multiplexer_20_out, multiplexer_22_out, multiplexer_24_out, multiplexer_25_out,
       multiplexer_33_out, not_1_out, operand, or_10_out, pIn_ptr, pRAM_readptr, regC_in, regC_in5, regC_in7,
       regC_in8, reset_ptr, result_ptr, rRAM_d2, rRAM_inD, rRAM_inptr, rRAM_readptr, sub_1_p3, xor_1_out;

  and and_1 (and_1_out, progLoad, t_ff_2_q);
  or or_1 (or_1_out, comparator_2_eq, and_1_out, reset);
  or or_2 (or_2_out, comparator_1_eq, result);
  T_FF t_ff_1 (.T(or_2_out), .C(clk), .Q(result_t));  // open: nQ
  T_FF t_ff_2 (.T(or_1_out), .C(clk), .Q(t_ff_2_q));  // open: nQ
  Counter #(.Bits(8)) counter_1 (.en(result_t), .C(clk), .clr(~result_t), .out(result_ptr));  // open: ovf
  Counter #(.Bits(8)) counter_2 (.en(progLoad), .C(clk), .clr(~progLoad), .out(pIn_ptr));  // open: ovf
  and and_2 (reset_t, t_ff_2_q, ~progLoad);  // And
  Comparator #(.Bits(8)) comparator_1 (.a(result_ptr), .b(8'he), .eq(comparator_1_eq));  // open: gt, lt
  Counter #(.Bits(8)) counter_3 (.en(reset_t), .C(clk), .clr(~reset_t), .out(reset_ptr));  // open: ovf
  and and_3 (and_3_out, ~opcode[4], ~opcode[3], ~opcode[2], ~opcode[1], ~opcode[0], start_t);  // And
  Comparator #(.Bits(8)) comparator_2 (.a(reset_ptr), .b(8'hfe), .eq(comparator_2_eq));  // open: gt, lt
  or or_3 (or_3_out, or_5_out, start);
  D_FF d_ff_1 (.D(and_3_out), .C(~clk), .Q(next0));  // open: nQ
  T_FF t_ff_3 (.T(or_3_out), .C(clk), .Q(start_t));  // open: nQ
  or or_4 (or_4_out, next, jump);
  or or_5 (or_5_out, comparator_3_eq, and_19_out);
  Multiplexer #(.Selector_Bits(2), .Bits(8)) multiplexer_1 (
    .sel({start_t, or_6_out[0]}), .in_0(pIn_ptr), .in_1(reset_ptr), .in_2(out_9), .in_3(jump_ptr), .out(out_5));
  Multiplexer #(.Bits(8)) multiplexer_2 (
    .sel(pRAM_isRead), .in_0({8{1'b0}}), .in_1(pRAM_readptr), .out(multiplexer_2_out));
  and and_4 (pRAM_isRead, ~opcode[4], opcode[3], ~opcode[2], ~opcode[1], opcode[0]);  // And
  D_FF #(.Bits(8)) d_ff_2 (.D(out_8), .C(clk), .Q(d_ff_2_q));  // open: nQ
  D_FF #(.Bits(8)) d_ff_3 (.D(out_12), .C(clk), .Q(d_ff_3_q));  // open: nQ
  Multiplexer #(.Bits(8)) multiplexer_3 (.sel(reset_t), .in_0(out_5), .in_1({8{1'b0}}), .out(multiplexer_3_out));
  RAMDualAccess #(.AddrBits(8), .Bits(13)) pRAM (
    .str(progLoad), .C(clk), .ld(start_t), .A1(out_5), .Din1(out_6), .A2(multiplexer_2_out), .D1(out_14),
    .D2(out_7));
  and and_5 (and_5_out, ~opcode[4], ~opcode[3], ~opcode[2], ~opcode[1], opcode[0]);  // And
  and and_6 (and_6_out, ~opcode[4], ~opcode[3], opcode[2], ~opcode[1], ~opcode[0]);  // And
  and and_7 (and_7_out, ~opcode[4], ~opcode[3], opcode[2], opcode[1], opcode[0]);  // And
  Multiplexer #(.Bits(8)) multiplexer_4 (.sel(pRAM_isRead), .in_0({8{1'b0}}), .in_1(operand), .out(pRAM_readptr));
  and and_8 (and_8_out, ~opcode[4], opcode[3], opcode[2]);  // And
  and and_9 (and_9_out, opcode[4], ~opcode[3], ~opcode[2], ~opcode[1], opcode[0]);  // And
  and and_10 (and_10_out, opcode[4], ~opcode[3], opcode[2], ~opcode[1]);  // And
  Add #(.Bits(8)) add_1 (.a(multiplexer_3_out), .b(8'h1), .c_i(1'b0), .s(add_1_s));  // open: c_o
  or or_6 (or_6_out[0], jump, reset_t);
  and and_11 (and_11_out, and_5_out, d_ff_17_nq, d_ff_5_nq);
  and and_12 (and_12_out, and_6_out, d_ff_18_nq, d_ff_7_nq);
  and and_13 (and_13_out, and_7_out, d_ff_19_nq, d_ff_9_nq);
  and and_14 (and_14_out, pRAM_isRead, d_ff_20_nq, d_ff_11_nq);
  Multiplexer #(.Selector_Bits(2)) multiplexer_5 (
    .sel(opcode[1:0]), .in_0(1'b1), .in_1(out_16), .in_2(out_15), .in_3(out_17), .out(multiplexer_5_out));
  Add #(.Bits(8)) add_2 (.a(out_8), .b(out_12), .c_i(1'b0), .s(add_2_s));  // open: c_o
  and and_15 (and_15_out, and_9_out, d_ff_23_nq, d_ff_13_nq);
  Div #(.Bits(8)) div_1 (.a(out_8), .b(out_12), .q(div_1_q), .r(div_1_r));
  and and_16 (and_16_out, and_10_out, d_ff_24_nq, d_ff_15_nq);
  and and_17 (and_17_out, or_4_out, start_t, clk);
  and and_18 (and_18_out, and_8_out, multiplexer_5_out);
  Multiplexer #(.Bits(8)) multiplexer_6 (.sel(opcode[0]), .in_0(div_1_q), .in_1(div_1_r), .out(multiplexer_6_out));
  and and_19 (and_19_out, opcode[0], opcode[1], opcode[2], opcode[3], opcode[4]);
  D_FF #(.Bits(8)) d_ff_4 (.D(operand), .C(clk), .Q(d_ff_4_q));  // open: nQ
  D_FF d_ff_5 (.D(and_11_out), .C(clk), .Q(accA_en1), .nQ(d_ff_5_nq));
  D_FF #(.Bits(8)) d_ff_6 (.D(out_8), .C(clk), .Q(d_ff_6_q));  // open: nQ
  D_FF d_ff_7 (.D(and_12_out), .C(clk), .Q(accB_en4), .nQ(d_ff_7_nq));
  D_FF #(.Bits(8)) d_ff_8 (.D(M), .C(clk), .Q(d_ff_8_q));  // open: nQ
  D_FF d_ff_9 (.D(and_13_out), .C(clk), .Q(regC_en7), .nQ(d_ff_9_nq));
  D_FF #(.Bits(8)) d_ff_10 (.D(out_7[7:0]), .C(clk), .Q(d_ff_10_q));  // open: nQ
  D_FF d_ff_11 (.D(and_14_out), .C(clk), .Q(accA_en9), .nQ(d_ff_11_nq));
  or or_7 (or_7_out, and_21_out, and_18_out);
  D_FF #(.Bits(8)) d_ff_12 (.D(add_2_s), .C(clk), .Q(d_ff_12_q));  // open: nQ
  D_FF d_ff_13 (.D(and_15_out), .C(clk), .Q(accA_en17), .nQ(d_ff_13_nq));
  D_FF #(.Bits(8)) d_ff_14 (.D(multiplexer_6_out), .C(clk), .Q(d_ff_14_q));  // open: nQ
  D_FF d_ff_15 (.D(and_16_out), .C(clk), .Q(accA_en1010X), .nQ(d_ff_15_nq));
  Multiplexer #(.Bits(8)) multiplexer_7 (.sel(start_t), .in_0({8{1'b0}}), .in_1(add_1_s), .out(multiplexer_7_out));
  or or_8 (or_8_out, ~start_t, and_17_out);  // Or
  Multiplexer #(.Bits(13)) multiplexer_8 (.sel(reset_t), .in_0(progIN), .in_1({13{1'b0}}), .out(out_6));
  Multiplexer #(.Bits(13)) multiplexer_9 (.sel(start_t), .in_0({13{1'b0}}), .in_1(out_14), .out({opcode, operand}));
  or or_9 (or_9_out, and_8_out, and_26_out);
  assign and_20_out = d_ff_2_q & d_ff_3_q;  // And and_20, 8 bits wide
  assign or_10_out = d_ff_2_q | d_ff_3_q;  // Or or_10, 8 bits wide
  assign xor_1_out = d_ff_2_q ^ d_ff_3_q;  // XOr xor_1, 8 bits wide
  Multiplexer #(.Bits(8)) multiplexer_10 (.sel(accA_en1), .in_0({8{1'b0}}), .in_1(d_ff_4_q), .out(accA_in1));
  Multiplexer #(.Bits(8)) multiplexer_11 (.sel(accB_en4), .in_0({8{1'b0}}), .in_1(d_ff_6_q), .out(accB_in4));
  Multiplexer #(.Bits(8)) multiplexer_12 (.sel(regC_en7), .in_0({8{1'b0}}), .in_1(d_ff_8_q), .out(regC_in7));
  Multiplexer #(.Bits(8)) multiplexer_13 (.sel(accA_en9), .in_0({8{1'b0}}), .in_1(d_ff_10_q), .out(accA_in9));
  and and_21 (and_21_out, or_11_out, and_26_out);
  and and_22 (and_22_out, or_7_out, d_ff_21_nq);
  Multiplexer #(.Bits(8)) multiplexer_14 (.sel(accA_en17), .in_0({8{1'b0}}), .in_1(d_ff_12_q), .out(accA_in17));
  Multiplexer #(.Bits(8)) multiplexer_15 (.sel(accA_en1010X), .in_0({8{1'b0}}), .in_1(d_ff_14_q), .out(accA_in1010X));
  and and_23 (and_23_out, opcode[4], opcode[3], ~opcode[2]);  // And
  D_FF #(.Bits(8)) d_ff_16 (.D(multiplexer_7_out), .C(or_8_out), .Q(d_ff_16_q));  // open: nQ
  and and_24 (and_24_out, or_9_out, ~or_7_out);  // And
  and and_25 (and_25_out, and_23_out, d_ff_28_nq, d_ff_26_nq);
  Comparator #(.Bits(8)) comparator_3 (.a(out_9), .b({8{1'b1}}), .eq(comparator_3_eq));  // open: gt, lt
  Multiplexer #(.Bits(8)) multiplexer_16 (.sel(jump), .in_0(d_ff_16_q), .in_1(jump_ptr), .out(out_9));
  D_FF d_ff_17 (.D(accA_en1), .C(~clk), .Q(next1), .nQ(d_ff_17_nq));
  D_FF d_ff_18 (.D(accB_en4), .C(~clk), .Q(next4), .nQ(d_ff_18_nq));
  D_FF d_ff_19 (.D(regC_en7), .C(~clk), .Q(next7), .nQ(d_ff_19_nq));
  D_FF d_ff_20 (.D(accA_en9), .C(~clk), .Q(next9), .nQ(d_ff_20_nq));
  and and_26 (and_26_out, ~opcode[0], ~opcode[1], ~opcode[2], ~opcode[3], opcode[4]);  // And
  or or_11 (or_11_out, out_15, out_16);
  D_FF d_ff_21 (.D(and_22_out), .C(clk), .Q(jump), .nQ(d_ff_21_nq));
  D_FF #(.Bits(8)) d_ff_22 (.D(operand), .C(clk), .Q(d_ff_22_q));  // open: nQ
  D_FF d_ff_23 (.D(accA_en17), .C(~clk), .Q(next17), .nQ(d_ff_23_nq));
  D_FF d_ff_24 (.D(accA_en1010X), .C(~clk), .Q(next1010X), .nQ(d_ff_24_nq));
  or or_12 (or_12_out, rRAM_inen, reset_t);
  Multiplexer #(.Bits(8)) multiplexer_17 (.sel(reset_t), .in_0(rRAM_inptr), .in_1(reset_ptr), .out(multiplexer_17_out));
  Multiplexer #(.Bits(8)) multiplexer_18 (.sel(reset_t), .in_0(rRAM_inD), .in_1({8{1'b0}}), .out(multiplexer_18_out));
  D_FF d_ff_25 (.D(and_24_out), .C(~clk), .Q(d_ff_25_q));  // open: nQ
  Multiplexer #(.Bits(8)) multiplexer_19 (.sel(jump), .in_0({8{1'b0}}), .in_1(d_ff_22_q), .out(jump_ptr));
  Multiplexer #(.Selector_Bits(2), .Bits(8)) multiplexer_20 (
    .sel(opcode[1:0]), .in_0(not_1_out), .in_1(and_20_out), .in_2(or_10_out), .in_3(xor_1_out),
    .out(multiplexer_20_out));
  assign not_1_out = ~d_ff_2_q;  // Not not_1, 8 bits wide
  D_FF d_ff_26 (.D(and_25_out), .C(clk), .Q(accA_enbitwise), .nQ(d_ff_26_nq));
  or or_13 (or_13_out, accA_en, reset_t);
  and and_27 (rRAM_isRead, ~opcode[4], opcode[3], ~opcode[2], opcode[1], ~opcode[0]);  // And
  and and_28 (and_28_out, d_ff_25_q, d_ff_21_nq);
  Multiplexer #(.Bits(8)) multiplexer_21 (
    .sel(accA_enbitwise), .in_0({8{1'b0}}), .in_1(multiplexer_20_out), .out(accA_inbitwise));
  Multiplexer #(.Bits(8)) multiplexer_22 (.sel(reset_t), .in_0(accA_in), .in_1({8{1'b0}}), .out(multiplexer_22_out));
  and and_29 (and_29_out, ~opcode[4], ~opcode[3], ~opcode[2], opcode[1], ~opcode[0]);  // And
  and and_30 (and_30_out, ~opcode[4], ~opcode[3], opcode[2], ~opcode[1], opcode[0]);  // And
  and and_31 (and_31_out, ~opcode[4], opcode[3], ~opcode[2], ~opcode[1], ~opcode[0]);  // And
  Multiplexer #(.Bits(8)) multiplexer_23 (.sel(rRAM_isRead), .in_0({8{1'b0}}), .in_1(operand), .out(rRAM_readptr));
  D_FF d_ff_27 (.D(and_28_out), .C(~clk), .Q(next_jump));  // open: nQ
  and and_32 (and_32_out, opcode[4], ~opcode[3], ~opcode[2], opcode[1], ~opcode[0]);  // And
  or or_14 (next, next0, next1, next2, next3, next4, next5, next6, next7, next8, next9, next_jump, next17, next18, next19, next1010X, next_bitwise, next28, next29, next23, next10, next11);
  Register #(.Bits(8)) accA (.D(multiplexer_22_out), .C(clk), .en(or_13_out), .Q(out_8));
  Multiplexer #(.Bits(8)) multiplexer_24 (
    .sel(rRAM_isRead), .in_0(result_ptr), .in_1(rRAM_readptr), .out(multiplexer_24_out));
  and and_33 (and_33_out, and_29_out, d_ff_39_nq, d_ff_30_nq);
  and and_34 (and_34_out, and_30_out, d_ff_40_nq, d_ff_32_nq);
  and and_35 (and_35_out, and_31_out, d_ff_41_nq, d_ff_34_nq);
  and and_36 (and_36_out, rRAM_isRead, d_ff_42_nq, d_ff_36_nq);
  // sub sub_1: pin names not known; wires that end beside it: out_8, out_12, sub_1_p3
  and and_37 (and_37_out, and_32_out, d_ff_43_nq, d_ff_38_nq);
  D_FF d_ff_28 (.D(accA_enbitwise), .C(~clk), .Q(next_bitwise), .nQ(d_ff_28_nq));
  RAMDualAccess #(.AddrBits(8), .Bits(8)) rRAM (
    .str(or_12_out), .C(clk), .ld(result_t), .A1(multiplexer_17_out), .Din1(multiplexer_18_out),
    .A2(multiplexer_24_out), .D2(rRAM_d2));  // open: D1
  D_FF #(.Bits(8)) d_ff_29 (.D(operand), .C(clk), .Q(d_ff_29_q));  // open: nQ
  D_FF d_ff_30 (.D(and_33_out), .C(clk), .Q(accB_en2), .nQ(d_ff_30_nq));
  D_FF #(.Bits(8)) d_ff_31 (.D(out_8), .C(clk), .Q(d_ff_31_q));  // open: nQ
  D_FF d_ff_32 (.D(and_34_out), .C(clk), .Q(regC_en5), .nQ(d_ff_32_nq));
  D_FF #(.Bits(8)) d_ff_33 (.D(N), .C(clk), .Q(d_ff_33_q));  // open: nQ
  D_FF d_ff_34 (.D(and_35_out), .C(clk), .Q(regC_en8), .nQ(d_ff_34_nq));
  D_FF #(.Bits(8)) d_ff_35 (.D(\output ), .C(clk), .Q(d_ff_35_q));  // open: nQ
  D_FF d_ff_36 (.D(and_36_out), .C(clk), .Q(accA_en10), .nQ(d_ff_36_nq));
  D_FF #(.Bits(8)) d_ff_37 (.D(sub_1_p3), .C(clk), .Q(d_ff_37_q));  // open: nQ
  D_FF d_ff_38 (.D(and_37_out), .C(clk), .Q(accA_en18), .nQ(d_ff_38_nq));
  assign accA_in = accA_in1 | accA_in3 | accA_in6 | accA_in9 | accA_in17 | accA_in18 | accA_in19 | accA_in1010X | accA_inbitwise | accA_in28 | accA_in10;  // Or or_15, 8 bits wide
  Multiplexer #(.Bits(8)) multiplexer_25 (.sel(reset_t), .in_0(accB_in), .in_1({8{1'b0}}), .out(multiplexer_25_out));
  or or_16 (or_16_out, accB_en, reset_t);
  Multiplexer #(.Bits(8)) multiplexer_26 (.sel(result_t), .in_0({8{1'b0}}), .in_1(rRAM_d2), .out(\output ));
  Register #(.Bits(8)) accB (.D(multiplexer_25_out), .C(clk), .en(or_16_out), .Q(out_12));
  Multiplexer #(.Bits(8)) multiplexer_27 (.sel(accB_en2), .in_0({8{1'b0}}), .in_1(d_ff_29_q), .out(accB_in2));
  Multiplexer #(.Bits(8)) multiplexer_28 (.sel(regC_en5), .in_0({8{1'b0}}), .in_1(d_ff_31_q), .out(regC_in5));
  Multiplexer #(.Bits(8)) multiplexer_29 (.sel(regC_en8), .in_0({8{1'b0}}), .in_1(d_ff_33_q), .out(regC_in8));
  Multiplexer #(.Bits(8)) multiplexer_30 (.sel(accA_en10), .in_0({8{1'b0}}), .in_1(d_ff_35_q), .out(accA_in10));
  Multiplexer #(.Bits(8)) multiplexer_31 (.sel(accA_en18), .in_0({8{1'b0}}), .in_1(d_ff_37_q), .out(accA_in18));
  Comparator #(.Bits(8)) comparator_4 (.a(out_12), .b(8'h8), .gt(comparator_4_gt));  // open: eq, lt
  and and_38 (and_38_out, opcode[4], opcode[3], opcode[2], ~opcode[1], ~opcode[0]);  // And
  D_FF d_ff_39 (.D(accB_en2), .C(~clk), .Q(next2), .nQ(d_ff_39_nq));
  D_FF d_ff_40 (.D(regC_en5), .C(~clk), .Q(next5), .nQ(d_ff_40_nq));
  D_FF d_ff_41 (.D(regC_en8), .C(~clk), .Q(next8), .nQ(d_ff_41_nq));
  D_FF d_ff_42 (.D(accA_en10), .C(~clk), .Q(next10), .nQ(d_ff_42_nq));
  D_FF d_ff_43 (.D(accA_en18), .C(~clk), .Q(next18), .nQ(d_ff_43_nq));
  Multiplexer #(.Bits(4)) multiplexer_32 (
    .sel(comparator_4_gt), .in_0(out_12[3:0]), .in_1(4'b1000), .out(multiplexer_32_out));
  and and_39 (and_39_out, and_38_out, d_ff_47_nq, d_ff_45_nq);
  or or_17 (accA_en, accA_en1, accA_en3, accA_en6, accA_en9, accA_en17, accA_en18, accA_en19, accA_en1010X, accA_enbitwise, accA_en28, accA_en10);
  or or_18 (or_18_out, regC_en, reset_t);
  BarrelShifter #(.Bits(8)) barrelshifter_1 (.in(out_8), .shift(multiplexer_32_out), .out(barrelshifter_1_out));
  Multiplexer #(.Bits(8)) multiplexer_33 (.sel(reset_t), .in_0(regC_in), .in_1({8{1'b0}}), .out(multiplexer_33_out));
  D_FF #(.Bits(8)) d_ff_44 (.D(barrelshifter_1_out), .C(clk), .Q(d_ff_44_q));  // open: nQ
  D_FF d_ff_45 (.D(and_39_out), .C(clk), .Q(accA_en28), .nQ(d_ff_45_nq));
  Register #(.Bits(8)) regC (.D(multiplexer_33_out), .C(clk), .en(or_18_out), .Q(out_13));
  and and_40 (and_40_out, ~opcode[4], opcode[3], ~opcode[2], opcode[1], opcode[0]);  // And
  assign accB_in = accB_in2 | accB_in4;  // Or or_19, 8 bits wide
  and and_41 (and_41_out, ~opcode[4], ~opcode[3], ~opcode[2], opcode[1], opcode[0]);  // And
  and and_42 (and_42_out, ~opcode[4], ~opcode[3], opcode[2], opcode[1], ~opcode[0]);  // And
  D_FF #(.Bits(8)) d_ff_46 (.D(operand), .C(clk), .Q(d_ff_46_q));  // open: nQ
  and and_43 (and_43_out, opcode[4], ~opcode[3], ~opcode[2], opcode[1], opcode[0]);  // And
  Multiplexer #(.Bits(8)) multiplexer_34 (.sel(accA_en28), .in_0({8{1'b0}}), .in_1(d_ff_44_q), .out(accA_in28));
  and and_44 (and_44_out, and_41_out, d_ff_58_nq, d_ff_49_nq);
  and and_45 (and_45_out, and_42_out, d_ff_59_nq, d_ff_51_nq);
  Multiplexer #(.Bits(8)) multiplexer_35 (.sel(and_40_out), .in_0({8{1'b0}}), .in_1(d_ff_46_q), .out(rRAM_inptr));
  and and_46 (and_46_out, and_40_out, d_ff_60_nq, d_ff_53_nq);
  Mul #(.Bits(4)) mul_1 (.a(out_8[3:0]), .b(out_12[3:0]), .mul(mul_1_mul));
  and and_47 (and_47_out, and_43_out, d_ff_61_nq, d_ff_55_nq);
  D_FF d_ff_47 (.D(accA_en28), .C(~clk), .Q(next28), .nQ(d_ff_47_nq));
  or or_20 (accB_en, accB_en2, accB_en4);
  and and_48 (and_48_out, start_q, ~start_t);  // And
  and and_49 (and_49_out, valid, result_t);
  D_FF #(.Bits(8)) d_ff_48 (.D(out_12), .C(clk), .Q(d_ff_48_q));  // open: nQ
  D_FF d_ff_49 (.D(and_44_out), .C(clk), .Q(accA_en3), .nQ(d_ff_49_nq));
  D_FF #(.Bits(8)) d_ff_50 (.D(out_13), .C(clk), .Q(d_ff_50_q));  // open: nQ
  D_FF d_ff_51 (.D(and_45_out), .C(clk), .Q(accA_en6), .nQ(d_ff_51_nq));
  D_FF #(.Bits(8)) d_ff_52 (.D(out_8), .C(clk), .Q(d_ff_52_q));  // open: nQ
  D_FF d_ff_53 (.D(and_46_out), .C(clk), .Q(rRAM_inen), .nQ(d_ff_53_nq));
  D_FF #(.Bits(8)) d_ff_54 (.D(mul_1_mul), .C(clk), .Q(d_ff_54_q));  // open: nQ
  D_FF d_ff_55 (.D(and_47_out), .C(clk), .Q(accA_en19), .nQ(d_ff_55_nq));
  D_FF u_start (.D(start_t), .C(clk), .Q(start_q));  // open: nQ
  D_FF d_ff_56 (.D(and_48_out), .C(clk), .Q(d_ff_56_q));  // open: nQ
  D_FF d_ff_57 (.D(and_49_out), .C(clk), .Q(d_ff_57_q));  // open: nQ
  Multiplexer #(.Bits(8)) multiplexer_36 (.sel(accA_en3), .in_0({8{1'b0}}), .in_1(d_ff_48_q), .out(accA_in3));
  Multiplexer #(.Bits(8)) multiplexer_37 (.sel(accA_en6), .in_0({8{1'b0}}), .in_1(d_ff_50_q), .out(accA_in6));
  Multiplexer #(.Bits(8)) multiplexer_38 (.sel(rRAM_inen), .in_0({8{1'b0}}), .in_1(d_ff_52_q), .out(rRAM_inD));
  and and_50 (and_50_out, opcode[4], ~opcode[3], opcode[2], opcode[1], opcode[0]);  // And
  Multiplexer #(.Bits(8)) multiplexer_39 (.sel(accA_en19), .in_0({8{1'b0}}), .in_1(d_ff_54_q), .out(accA_in19));
  and and_51 (and_51_out, opcode[4], opcode[3], opcode[2], ~opcode[1], opcode[0]);  // And
  assign regC_in = regC_in5 | regC_in7 | regC_in8;  // Or or_21, 8 bits wide
  and and_52 (and_52_out, start, valid);
  or or_22 (or_22_out, and_52_out, d_ff_56_q);
  and and_53 (and_53_out, d_ff_57_q, ~result_t);  // And
  D_FF d_ff_58 (.D(accA_en3), .C(~clk), .Q(next3), .nQ(d_ff_58_nq));
  D_FF d_ff_59 (.D(accA_en6), .C(~clk), .Q(next6), .nQ(d_ff_59_nq));
  D_FF d_ff_60 (.D(rRAM_inen), .C(~clk), .Q(next11), .nQ(d_ff_60_nq));
  D_FF d_ff_61 (.D(accA_en19), .C(~clk), .Q(next19), .nQ(d_ff_61_nq));
  and and_54 (and_54_out, clk, and_51_out);
  T_FF t_ff_4 (.T(or_22_out), .C(clk), .Q(valid));  // open: nQ
  and and_55 (and_55_out, start, done);
  and and_56 (and_56_out, and_50_out, d_ff_65_nq, d_ff_64_nq);
  // isprime isprime_1: pin names not known; wires that end beside it: out_8, isprime_1_p2
  and and_57 (and_57_out, and_51_out, d_ff_66_nq, d_ff_63_nq);
  or or_23 (regC_en, regC_en5, regC_en7, regC_en8);
  or or_24 (or_24_out, and_53_out, and_55_out);
  D_FF d_ff_62 (.D(isprime_1_p2), .C(and_54_out), .Q(equal29));  // open: nQ
  D_FF d_ff_63 (.D(and_57_out), .C(clk), .Q(d_ff_63_q), .nQ(d_ff_63_nq));
  T_FF t_ff_5 (.T(or_24_out), .C(clk), .Q(done));  // open: nQ
  Comparator #(.Bits(8)) comparator_5 (
    .a(out_8), .b(out_12), .gt(comparator_5_gt), .eq(comparator_5_eq), .lt(comparator_5_lt));
  D_FF d_ff_64 (.D(and_56_out), .C(clk), .Q(d_ff_64_q), .nQ(d_ff_64_nq));
  or or_25 (out_16, equal23, equal29);
  D_FF d_ff_65 (.D(d_ff_64_q), .C(~clk), .Q(next23), .nQ(d_ff_65_nq));
  D_FF d_ff_66 (.D(d_ff_63_q), .C(~clk), .Q(next29), .nQ(d_ff_66_nq));
  or or_26 (or_26_out, reset_t, d_ff_64_q);
  or or_27 (or_27_out, reset_t, d_ff_64_q);
  Multiplexer multiplexer_40 (.sel(reset_t), .in_0(comparator_5_gt), .in_1(1'b0), .out(multiplexer_40_out));
  Multiplexer multiplexer_41 (.sel(reset_t), .in_0(comparator_5_eq), .in_1(1'b0), .out(multiplexer_41_out));
  Multiplexer multiplexer_42 (.sel(reset_t), .in_0(comparator_5_lt), .in_1(1'b0), .out(multiplexer_42_out));
  or or_28 (or_28_out, reset_t, d_ff_64_q);
  D_FF d_ff_67 (.D(multiplexer_40_out), .C(or_26_out), .Q(out_15));  // open: nQ
  D_FF d_ff_68 (.D(multiplexer_41_out), .C(or_27_out), .Q(equal23));  // open: nQ
  D_FF d_ff_69 (.D(multiplexer_42_out), .C(or_28_out), .Q(out_17));  // open: nQ

  // Other names for the same wires on the sheet: accA_out[7:0] = out_8; accB_out[7:0] = out_12; equal = out_16;
  //   greater = out_15; lesser = out_17; next_ptr[7:0] = out_9; pRAM_read[7:0] = out_7[7:0]; pIn[12:0] = progIN;
  //   pLoad = progLoad; pRAM_A[7:0] = out_5; pRAM_in[12:0] = out_6; regC_out[7:0] = out_13; send_reset = reset;
  //   send_result = result; send_start = start

  // Notes on the sheet:
  //   result
  //   reset
  //   Input
  //   Operation
  //   progIn
  //   00000 (NONE)
  //   debug
  //   start
  //   pRAM_A
  //   Main Memory
  //   00001 (accA ← Operand)
  //   00100 (accB ← accA)
  //   00111 (regC ← M)
  //   01001 (accA ← pRAM_adr[Operand])
  //   011XX - 10000 (Jump to address Operand)
  //   10001 (accA ← accA + accB)
  //   1010X (accA ← accA / accB) && (accA ← accA % accB)
  //   110XX (Bitwise)
  //   pRAM_in
  //   00010 (accB ← Operand)
  //   00101 (regC ← accA)
  //   01000 (regC ← N)
  //   01010 (accA ← rRAM_adr[Operand])
  //   10010 (accA ← accA - accB)
  //   accA
  //   accB
  //   11100 (accA ←  accA << accB)
  //   00011 (accA ← accB)
  //   00110 (accA ← regC)
  //   01011 (rRAM_adr[Operand] ← accA)
  //   10011 (accA ← accA * accB)
  //   CPU-State
  //   10111 (accA CMP accB)
  //   11101 (isPrime(accA))
endmodule

/* Test case:
M N progIN reset progLoad start result clk valid done output
0 0 0 0 0 0 0 0 0 0 0
0 0 0 0 0 0 0 1 0 0 0
0 0 0 1 0 0 0 0 0 0 0
0 0 0 1 0 0 0 1 0 0 0
0 0 0 0 0 0 0 0 0 0 0
0 0 0 0 0 0 0 1 0 0 0
0 0 0 0 0 0 0 0 0 0 0
0 0 0 0 0 0 0 1 0 0 0
0 0 0 0 0 0 0 0 0 0 0
0 0 0 0 0 0 0 1 0 0 0
0 0 0 0 0 0 0 0 0 0 0
0 0 0 0 0 0 0 1 0 0 0
0 0 0 0 0 0 0 0 0 0 0
0 0 0 0 0 0 0 1 0 0 0
0 0 0 0 0 0 0 0 0 0 0
0 0 0 0 0 0 0 1 0 0 0
0 0 0 0 0 0 0 0 0 0 0
0 0 0 0 0 0 0 1 0 0 0
0 0 0 0 0 0 0 0 0 0 0
0 0 0 0 0 0 0 1 0 0 0
0 0 0 0 0 0 0 0 0 0 0
0 0 0 0 0 0 0 1 0 0 0
0 0 0 0 0 0 0 0 0 0 0
0 0 0 0 0 0 0 1 0 0 0
0 0 0 0 0 0 0 0 0 0 0
0 0 0 0 0 0 0 1 0 0 0
0 0 0 0 0 0 0 0 0 0 0
0 0 0 0 0 0 0 1 0 0 0
0 0 0 0 0 0 0 0 0 0 0
0 0 0 0 0 0 0 1 0 0 0
0 0 0 0 0 0 0 0 0 0 0
0 0 0 0 0 0 0 1 0 0 0
0 0 0 0 0 0 0 0 0 0 0
0 0 0 0 0 0 0 1 0 0 0
0 0 0 0 0 0 0 0 0 0 0
0 0 0 0 0 0 0 1 0 0 0
0 0 0 0 0 0 0 0 0 0 0
0 0 0 0 0 0 0 1 0 0 0
0 0 0 0 0 0 0 0 0 0 0
0 0 0 0 0 0 0 1 0 0 0
0 0 0 0 0 0 0 0 0 0 0
0 0 0 0 0 0 0 1 0 0 0
0 0 271 0 1 0 0 0 0 0 0
0 0 0 0 1 0 0 1 0 0 0
0 0 565 0 1 0 0 0 0 0 0
0 0 0 0 1 0 0 1 0 0 0
0 0 4352 0 1 0 0 0 0 0 0
0 0 0 0 1 0 0 1 0 0 0
0 0 2819 0 1 0 0 0 0 0 0
0 0 0 0 1 0 0 1 0 0 0
0 0 7936 0 1 0 0 0 0 0 0
0 0 0 0 1 0 0 1 0 0 0
0 0 0 0 0 1 0 0 0 0 0
0 0 0 0 0 1 0 1 0 0 0
0 0 0 0 0 0 0 0 x 0 0
0 0 0 0 0 0 0 1 x 0 0
0 0 0 0 0 0 0 0 x 0 0
0 0 0 0 0 0 0 1 x 0 0
0 0 0 0 0 0 0 0 x 0 0
0 0 0 0 0 0 0 1 x 0 0
0 0 0 0 0 0 0 0 x 0 0
0 0 0 0 0 0 0 1 x 0 0
0 0 0 0 0 0 0 0 x 0 0
0 0 0 0 0 0 0 1 x 0 0
0 0 0 0 0 0 0 0 x 0 0
0 0 0 0 0 0 0 1 x 0 0
0 0 0 0 0 0 0 0 x 0 0
0 0 0 0 0 0 0 1 x 0 0
0 0 0 0 0 0 0 0 x 0 0
0 0 0 0 0 0 0 1 x 0 0
0 0 0 0 0 0 0 0 x 0 0
0 0 0 0 0 0 0 1 x 0 0
0 0 0 0 0 0 0 0 x 0 0
0 0 0 0 0 0 0 1 x 0 0
0 0 0 0 0 0 0 0 x 0 0
0 0 0 0 0 0 0 1 x 0 0
0 0 0 0 0 0 0 0 x 0 0
0 0 0 0 0 0 0 1 x 0 0
0 0 0 0 0 0 0 0 x 0 0
0 0 0 0 0 0 0 1 x 0 0
0 0 0 0 0 0 0 0 x 0 0
0 0 0 0 0 0 0 1 x 0 0
0 0 0 0 0 0 0 0 x 0 0
0 0 0 0 0 0 0 1 x 0 0
0 0 0 0 0 0 0 0 x 0 0
0 0 0 0 0 0 0 1 x 0 0
0 0 0 0 0 0 0 0 x 0 0
0 0 0 0 0 0 0 1 x 0 0
0 0 0 0 0 0 0 0 x 0 0
0 0 0 0 0 0 0 1 x 0 0
0 0 0 0 0 0 0 0 x 0 0
0 0 0 0 0 0 0 1 x 0 0
0 0 0 0 0 0 0 0 x 0 0
0 0 0 0 0 0 0 1 x 0 0
0 0 0 0 0 0 0 0 x 0 0
0 0 0 0 0 0 0 1 x 0 0
0 0 0 0 0 0 0 0 x 0 0
0 0 0 0 0 0 0 1 x 0 0
0 0 0 0 0 0 0 0 x 0 0
0 0 0 0 0 0 0 1 x 0 0
0 0 0 0 0 0 0 0 x 0 0
0 0 0 0 0 0 0 1 x 0 0
0 0 0 0 0 0 0 0 x 0 0
0 0 0 0 0 0 0 1 x 0 0
0 0 0 0 0 0 0 0 x 0 0
0 0 0 0 0 0 0 1 1 0 0
0 0 0 0 0 0 1 0 1 0 0
0 0 0 0 0 0 1 1 1 0 0
0 0 0 0 0 0 0 0 1 0 0
0 0 0 0 0 0 0 1 1 0 0
0 0 0 0 0 0 0 0 1 0 0
0 0 0 0 0 0 0 1 1 0 0
0 0 0 0 0 0 0 0 1 0 0
0 0 0 0 0 0 0 1 1 0 68
0 0 0 0 0 0 0 0 1 0 68
0 0 0 0 0 0 0 1 1 0 0
0 0 0 0 0 0 0 0 1 0 0
0 0 0 0 0 0 0 1 1 0 0
0 0 0 0 0 0 0 0 1 0 0
0 0 0 0 0 0 0 1 1 0 0
0 0 0 0 0 0 0 0 1 0 0
0 0 0 0 0 0 0 1 1 0 0
0 0 0 0 0 0 0 0 1 0 0
0 0 0 0 0 0 0 1 1 0 0
0 0 0 0 0 0 0 0 1 0 0
0 0 0 0 0 0 0 1 1 0 0
0 0 0 0 0 0 0 0 1 0 0
0 0 0 0 0 0 0 1 1 0 0
0 0 0 0 0 0 0 0 1 0 0
0 0 0 0 0 0 0 1 1 0 0
0 0 0 0 0 0 0 0 1 0 0
0 0 0 0 0 0 0 1 1 0 0
0 0 0 0 0 0 0 0 1 0 0
0 0 0 0 0 0 0 1 1 0 0
0 0 0 0 0 0 0 0 1 0 0
0 0 0 0 0 0 0 1 1 0 0
0 0 0 0 0 0 0 0 1 0 0
0 0 0 0 0 0 0 1 1 0 0
0 0 0 0 0 0 0 0 1 0 0
0 0 0 0 0 0 0 1 1 1 0
0 0 0 0 0 0 0 0 1 1 0
0 0 0 0 0 0 0 1 1 1 0
0 0 0 0 0 0 0 0 1 1 0
*/
