// Digital circuit project test1.dig as structural Verilog
module project_test1 (
  input  reset,
  input  clock,
  input  start,
  input  [12:0] progIN,
  input  progLoad,
  input  in_7,
  output [12:0] Data_bits_13,
  output [7:0] Z
);

  wire and_1_out, t_ff_1_q;
  wire [7:0] add_1_s, counter_1_out, multiplexer_1_out;

  and and_1 (and_1_out, start, ~t_ff_1_q);  // And
  Multiplexer #(.Bits(8)) multiplexer_1 (.sel(in_7), .in_0(add_1_s), .in_1(8'h4), .out(multiplexer_1_out));
  T_FF t_ff_1 (.T(and_1_out), .C(clock), .Q(t_ff_1_q));  // open: nQ
  Counter #(.Bits(8)) counter_1 (.en(progLoad), .C(clock), .clr(reset), .out(counter_1_out));  // open: ovf
  BlockRAMDualPort #(.AddrBits(1), .Bits(8)) blockramdualport_1 (
    .A(1'b0), .Din(multiplexer_1_out), .str(t_ff_1_q), .C(clock), .D(Z));
  Add #(.Bits(8)) add_1 (.a(Z), .b(8'h1), .c_i(1'b0), .s(add_1_s));  // open: c_o
  RAMDualAccess #(.AddrBits(8), .Bits(13)) ramdualaccess_1 (
    .str(1'b1), .C(clock), .ld(1'b0), .A1(counter_1_out), .Din1(progIN), .A2(Z), .D2(Data_bits_13));  // open: D1

  // Other names for the same wires on the sheet: clk = clock; pIn[12:0] = progIN; pLoad = progLoad

  // Notes on the sheet:
  //   Input
  //   Control Unit
  //   PC
endmodule
