// Digital circuit real_final.dig as structural Verilog
module real_final (
  input  [7:0] M,
  input  [7:0] N,
  input  [12:0] progIN,
  input  reset,
  input  progLoad,
  input  start,
  input  result,
  input  clk,
  input  [12:0] jump,
  input  meejumpmai,
  input  _1111,
  input  clock,
  input  _1111_2,
  input  PutInMem,
  input  [7:0] ValueInOp,
  output valid,
  output done,
  output [7:0] \output ,
  output [12:0] out_15,
  output [7:0] out_16,
  output [12:0] out_17,
  output [4:0] opcode,
  output [7:0] operand
);

  wire accAcheck, accAIn, accBcheck, accBIn, counting, start_t;
  wire [7:0] accAout, accBout, add_1_s, and_1_out, counter_1_out, multiplexer_1_out, multiplexer_2_out,
       multiplexer_3_out, multiplexer_4_out, multiplexer_5_out, multiplexer_6_out, undriven;

  and and_1 (and_1_out[0], start, ~start_t);  // And
  Multiplexer #(.Bits(8)) multiplexer_1 (.sel(_1111_2), .in_0(and_1_out), .in_1({8{1'b0}}), .out(multiplexer_1_out));
  T_FF t_ff_1 (.T(multiplexer_1_out[0]), .C(clock), .Q(start_t));  // open: nQ
  Counter #(.Bits(8)) counter_1 (.en(progLoad), .C(clock), .clr(1'b0), .out(counter_1_out), .ovf(counting));
  Sub sub_1 (.a(counting), .b(1'b1), .s(counting));  // open: c_i, c_o
  Multiplexer #(.Bits(8)) multiplexer_2 (.sel(meejumpmai), .in_0(add_1_s), .in_1(jump[7:0]), .out(multiplexer_2_out));
  Multiplexer multiplexer_3 (.sel(reset), .in_0(accAIn), .in_1(1'b0), .out(multiplexer_3_out[0]));
  Register #(.Bits(8)) accA (.D(multiplexer_3_out), .C(clock), .en(accAcheck), .Q(accAout));
  Multiplexer multiplexer_4 (.sel(reset), .in_0(accBIn), .in_1(1'b0), .out(multiplexer_4_out[0]));
  Register #(.Bits(8)) accB (.D(multiplexer_4_out), .C(clock), .en(accBcheck), .Q(accBout));
  Multiplexer #(.Bits(8)) multiplexer_5 (
    .sel(_1111), .in_0(multiplexer_2_out), .in_1({8{1'b0}}), .out(multiplexer_5_out));
  Decoder decoder_1 ();  // open: sel, out_0, out_1
  Multiplexer #(.Bits(8)) multiplexer_6 (
    .sel(reset), .in_0(multiplexer_5_out), .in_1({8{1'b0}}), .out(multiplexer_6_out));
  BlockRAMDualPort #(.AddrBits(8), .Bits(8)) PC (
    .A({8{1'b0}}), .Din(multiplexer_6_out), .str(start_t), .C(clock), .D(out_16));
  RAMDualAccess #(.AddrBits(8), .Bits(13)) pRAM (
    .str(progLoad), .C(clock), .ld(start_t), .Din1(progIN), .A2(out_16), .D1(out_15), .D2({opcode, operand}));  // open: A1
  RAMDualAccess #(.AddrBits(8), .Bits(8)) rRAM (
    .str(PutInMem), .C(clock), .ld(PutInMem), .A1(undriven), .Din1(ValueInOp));  // open: A2, D1, D2
  Add #(.Bits(8)) add_1 (.a(8'h1), .b(out_16), .c_i(1'b0), .s(add_1_s));  // open: c_o
  // And and_2 has open pins: In_1=opcode[0], In_2=opcode[1], In_3=opcode[2], In_4=opcode[3], In_5=opcode[4], out=open
  // And and_3 has open pins: In_1=opcode[0], In_2=opcode[1], In_3=opcode[2], In_4=opcode[3], In_5=opcode[4], out=open
  Seven_Seg_Hex seven_seg_hex_1 (.d(jump[7:4]), .dp(1'b0));
  Seven_Seg_Hex seven_seg_hex_2 (.d(jump[3:0]), .dp(1'b0));
  // Pins of 1 and 8 bits meet at multiplexer_1_out
  // Pins of 1 and 8 bits meet at and_1_out
  // Pins of 1 and 8 bits meet at ValueInOp
  // Pins of 1 and 8 bits meet at multiplexer_3_out
  // Pins of 1 and 8 bits meet at {8{1'b0}}
  // Pins of 1 and 8 bits meet at multiplexer_4_out
  // Pins of 1 and 8 bits meet at {8{1'b0}}
  // Pins of 1 and 8 bits meet at 8'h1

  assign done = reset;
  assign out_17 = {opcode, operand};
  assign valid = reset;

  // Other names for the same wires on the sheet: clk_t = clock; jkhkhkj[4:0] = jump[12:8]; pc[7:0] = out_16;
  //   Pin[12:0] = progIN; Pload = progLoad

  // Notes on the sheet:
  //   start
  //   input
  //   loadPin
  //   minusPin
  //   PC
  //   regis
  //   FIx plz
  //   IR
  //   memoryRram
  //   out
endmodule

/* Test case 01_P01T01:
M N progIN reset progLoad start result clk valid done output
0 0 0 0 0 0 0 0 0 0 0
0 0 0 0 0 0 0 1 0 0 0
0 0 0 1 0 0 0 0 0 0 0
0 0 0 1 0 0 0 1 0 0 0
0 0 0 0 0 0 0 0 0 0 0
0 0 0 0 0 0 0 1 0 0 0
0 0 0 0 0 0 0 0 0 0 0
0 0 0 0 0 0 0 1 0 0 0
0 0 0 0 0 0 0 0 0 0 0
0 0 0 0 0 0 0 1 0 0 0
0 0 0 0 0 0 0 0 0 0 0
0 0 0 0 0 0 0 1 0 0 0
0 0 0 0 0 0 0 0 0 0 0
0 0 0 0 0 0 0 1 0 0 0
0 0 0 0 0 0 0 0 0 0 0
0 0 0 0 0 0 0 1 0 0 0
0 0 0 0 0 0 0 0 0 0 0
0 0 0 0 0 0 0 1 0 0 0
0 0 0 0 0 0 0 0 0 0 0
0 0 0 0 0 0 0 1 0 0 0
0 0 0 0 0 0 0 0 0 0 0
0 0 0 0 0 0 0 1 0 0 0
0 0 0 0 0 0 0 0 0 0 0
0 0 0 0 0 0 0 1 0 0 0
0 0 0 0 0 0 0 0 0 0 0
0 0 0 0 0 0 0 1 0 0 0
0 0 0 0 0 0 0 0 0 0 0
0 0 0 0 0 0 0 1 0 0 0
0 0 0 0 0 0 0 0 0 0 0
0 0 0 0 0 0 0 1 0 0 0
0 0 0 0 0 0 0 0 0 0 0
0 0 0 0 0 0 0 1 0 0 0
0 0 0 0 0 0 0 0 0 0 0
0 0 0 0 0 0 0 1 0 0 0
0 0 0 0 0 0 0 0 0 0 0
0 0 0 0 0 0 0 1 0 0 0
0 0 0 0 0 0 0 0 0 0 0
0 0 0 0 0 0 0 1 0 0 0
0 0 0 0 0 0 0 0 0 0 0
0 0 0 0 0 0 0 1 0 0 0
0 0 0 0 0 0 0 0 0 0 0
0 0 0 0 0 0 0 1 0 0 0
0 0 271 0 1 0 0 0 0 0 0
0 0 0 0 1 0 0 1 0 0 0
0 0 565 0 1 0 0 0 0 0 0
0 0 0 0 1 0 0 1 0 0 0
0 0 4352 0 1 0 0 0 0 0 0
0 0 0 0 1 0 0 1 0 0 0
0 0 2819 0 1 0 0 0 0 0 0
0 0 0 0 1 0 0 1 0 0 0
0 0 7936 0 1 0 0 0 0 0 0
0 0 0 0 1 0 0 1 0 0 0
0 0 0 0 0 1 0 0 0 0 0
0 0 0 0 0 1 0 1 0 0 0
0 0 0 0 0 0 0 0 x 0 0
0 0 0 0 0 0 0 1 x 0 0
0 0 0 0 0 0 0 0 x 0 0
0 0 0 0 0 0 0 1 x 0 0
0 0 0 0 0 0 0 0 x 0 0
0 0 0 0 0 0 0 1 x 0 0
0 0 0 0 0 0 0 0 x 0 0
0 0 0 0 0 0 0 1 x 0 0
0 0 0 0 0 0 0 0 x 0 0
0 0 0 0 0 0 0 1 x 0 0
0 0 0 0 0 0 0 0 x 0 0
0 0 0 0 0 0 0 1 x 0 0
0 0 0 0 0 0 0 0 x 0 0
0 0 0 0 0 0 0 1 x 0 0
0 0 0 0 0 0 0 0 x 0 0
0 0 0 0 0 0 0 1 x 0 0
0 0 0 0 0 0 0 0 x 0 0
0 0 0 0 0 0 0 1 x 0 0
0 0 0 0 0 0 0 0 x 0 0
0 0 0 0 0 0 0 1 x 0 0
0 0 0 0 0 0 0 0 x 0 0
0 0 0 0 0 0 0 1 x 0 0
0 0 0 0 0 0 0 0 x 0 0
0 0 0 0 0 0 0 1 x 0 0
0 0 0 0 0 0 0 0 x 0 0
0 0 0 0 0 0 0 1 x 0 0
0 0 0 0 0 0 0 0 x 0 0
0 0 0 0 0 0 0 1 x 0 0
0 0 0 0 0 0 0 0 x 0 0
0 0 0 0 0 0 0 1 x 0 0
0 0 0 0 0 0 0 0 x 0 0
0 0 0 0 0 0 0 1 x 0 0
0 0 0 0 0 0 0 0 x 0 0
0 0 0 0 0 0 0 1 x 0 0
0 0 0 0 0 0 0 0 x 0 0
0 0 0 0 0 0 0 1 x 0 0
0 0 0 0 0 0 0 0 x 0 0
0 0 0 0 0 0 0 1 x 0 0
0 0 0 0 0 0 0 0 x 0 0
0 0 0 0 0 0 0 1 x 0 0
0 0 0 0 0 0 0 0 x 0 0
0 0 0 0 0 0 0 1 x 0 0
0 0 0 0 0 0 0 0 x 0 0
0 0 0 0 0 0 0 1 x 0 0
0 0 0 0 0 0 0 0 x 0 0
0 0 0 0 0 0 0 1 x 0 0
0 0 0 0 0 0 0 0 x 0 0
0 0 0 0 0 0 0 1 x 0 0
0 0 0 0 0 0 0 0 x 0 0
0 0 0 0 0 0 0 1 x 0 0
0 0 0 0 0 0 0 0 x 0 0
0 0 0 0 0 0 0 1 1 0 0
0 0 0 0 0 0 1 0 1 0 0
0 0 0 0 0 0 1 1 1 0 0
0 0 0 0 0 0 0 0 1 0 0
0 0 0 0 0 0 0 1 1 0 0
0 0 0 0 0 0 0 0 1 0 0
0 0 0 0 0 0 0 1 1 0 0
0 0 0 0 0 0 0 0 1 0 0
0 0 0 0 0 0 0 1 1 0 68
0 0 0 0 0 0 0 0 1 0 68
0 0 0 0 0 0 0 1 1 0 0
0 0 0 0 0 0 0 0 1 0 0
0 0 0 0 0 0 0 1 1 0 0
0 0 0 0 0 0 0 0 1 0 0
0 0 0 0 0 0 0 1 1 0 0
0 0 0 0 0 0 0 0 1 0 0
0 0 0 0 0 0 0 1 1 0 0
0 0 0 0 0 0 0 0 1 0 0
0 0 0 0 0 0 0 1 1 0 0
0 0 0 0 0 0 0 0 1 0 0
0 0 0 0 0 0 0 1 1 0 0
0 0 0 0 0 0 0 0 1 0 0
0 0 0 0 0 0 0 1 1 0 0
0 0 0 0 0 0 0 0 1 0 0
0 0 0 0 0 0 0 1 1 0 0
0 0 0 0 0 0 0 0 1 0 0
0 0 0 0 0 0 0 1 1 0 0
0 0 0 0 0 0 0 0 1 0 0
0 0 0 0 0 0 0 1 1 0 0
0 0 0 0 0 0 0 0 1 0 0
0 0 0 0 0 0 0 1 1 0 0
0 0 0 0 0 0 0 0 1 0 0
0 0 0 0 0 0 0 1 1 0 0
0 0 0 0 0 0 0 0 1 0 0
0 0 0 0 0 0 0 1 1 1 0
0 0 0 0 0 0 0 0 1 1 0
0 0 0 0 0 0 0 1 1 1 0
0 0 0 0 0 0 0 0 1 1 0
*/
