// Digital circuit rom.dig as structural Verilog
module rom (
);

  wire lll;
  wire [7:0] \output , output1;

  ROM #(.AddrBits(16), .Bits(16)) rom_1 (.A({output1, \output }), .sel(lll));  // open: D

  // Notes on the sheet:
  //   contents of rom_1 (hex, n*v repeats v):
  //   257*0,1,2,3,4,5,6,7,8,9,a,b,c,d,e,f,10,11,12,13,14,15,16,17,18
  //   ,19,1a,1b,1c,1d,1e,1f,20,21,22,23,24,25,26,27,28,29,2a,2b,2c,2d
  //   ,2e,2f,30,31,32,33,34,35,36,37,38,39,3a,3b,3c,3d,3e,3f,40,41,42
  //   ,43,44,45,46,47,48,49,4a,4b,4c,4d,4e,4f,50,51,52,53,54,55,56,57
  //   ,58,59,5a,5b,5c,5d,5e,5f,60,61,62,63,64,65,66,67,68,69,6a,6b,6c
  //   ,6d,6e,6f,70,71,72,73,74,75,76,77,78,79,7a,7b,7c,7d,7e,7f,80,81
  //   ,82,83,84,85,86,87,88,89,8a,8b,8c,8d,8e,8f,90,91,92,93,94,95,96
  //   ,97,98,99,9a,9b,9c,9d,9e,9f,a0,a1,a2,a3,a4,a5,a6,a7,a8,a9,aa,ab
  //   ,ac,ad,ae,af,b0,b1,b2,b3,b4,b5,b6,b7,b8,b9,ba,bb,bc,bd,be,bf,c0
  //   ,c1,c2,c3,c4,c5,c6,c7,c8,c9,ca,cb,cc,cd,ce,cf,d0,d1,d2,d3,d4,d5
  //   ,d6,d7,d8,d9,da,db,dc,dd,de,df,e0,e1,e2,e3,e4,e5,e6,e7,e8,e9,ea
  //   ,eb,ec,ed,ee,ef,f0,f1,f2,f3,f4,f5,f6,f7,f8,f9,fa,fb,fc,fd,fe,ff
  //   ,0,2,2,6,4,a,6,e,8,12,a,16,c,1a,e,1e,10,22,12,26,14,2a,16,2e,18
  //   ,32,1a,36,1c,3a,1e,3e,20,42,22,46,24,4a,26,4e,28,52,2a,56,2c,5a
  //   ,2e,5e,30,62,32,66,34,6a,36,6e,38,72,3a,76,3c,7a,3e,7e,40,82,42
  //   ,86,44,8a,46,8e,48,92,4a,96,4c,9a,4e,9e,50,a2,52,a6,54,aa,56,ae
  //   ,58,b2,5a,b6,5c,ba,5e,be,60,c2,62,c6,64,ca,66,ce,68,d2,6a,d6,6c
  //   ,da,6e,de,70,e2,72,e6,74,ea,76,ee,78,f2,7a,f6,7c,fa,7e,fe,80,102
  //   ,82,106,84,10a,86,10e,88,112,8a,116,8c,11a,8e,11e,90,122,92,126
  //   ,94,12a,96,12e,98,132,9a,136,9c,13a,9e,13e,a0,142,a2,146,a4,14a
  //   ,a6,14e,a8,152,aa,156,ac,15a,ae,15e,b0,162,b2,166,b4,16a,b6,16e
  //   ,b8,172,ba,176,bc,17a,be,17e,c0,182,c2,186,c4,18a,c6,18e,c8,192
  //   ,ca,196,cc,19a,ce,19e,d0,1a2,d2,1a6,d4,1aa,d6,1ae,d8,1b2,da,1b6
  //   ,dc,1ba,de,1be,e0,1c2,e2,1c6,e4,1ca,e6,1ce,e8,1d2,ea,1d6,ec,1da
  //   ,ee,1de,f0,1e2,f2,1e6,f4,1ea,f6,1ee,f8,1f2,fa,1f6,fc,1fa,fe,1fe
  //   ,0,3,6,3,c,f,6,15,18,9,1e,21,c,27,2a,f,30,33,12,39,3c,15,42,45
  //   ,18,4b,4e,1b,54,57,1e,5d,60,21,66,69,24,6f,72,27,78,7b,2a,81,84
  //   ,2d,8a,8d,30,93,96,33,9c,9f,36,a5,a8,39,ae,b1,3c,b7,ba,3f,c0,c3
  //   ,42,c9,cc,45,d2,d5,48,db,de,4b,e4,e7,4e,ed,f0,51,f6,f9,54,ff,102
  //   ,57,108,10b,5a,111,114,5d,11a,11d,60,123,126,63,12c,12f,66,135
  //   ,138,69,13e,141,6c,147,14a,6f,150,153,72,159,15c,75,162,165,78
  //   ,16b,16e,7b,174,177,7e,17d,180,81,186,189,84,18f,192,87,198,19b
  //   ,8a,1a1,1a4,8d,1aa,1ad,90,1b3,1b6,93,1bc,1bf,96,1c5,1c8,99,1ce
  //   ,1d1,9c,1d7,1da,9f,1e0,1e3,a2,1e9,1ec,a5,1f2,1f5,a8,1fb,1fe,ab
  //   ,204,207,ae,20d,210,b1,216,219,b4,21f,222,b7,228,22b,ba,231,234
  //   ,bd,23a,23d,c0,243,246,c3,24c,24f,c6,255,258,c9,25e,261,cc,267
  //   ,26a,cf,270,273,d2,279,27c,d5,282,285,d8,28b,28e,db,294,297,de
  //   ,29d,2a0,e1,2a6,2a9,e4,2af,2b2,e7,2b8,2bb,ea,2c1,2c4,ed,2ca,2cd
  //   ,f0,2d3,2d6,f3,2dc,2df,f6,2e5,2e8,f9,2ee,2f1,fc,2f7,2fa,ff,0,4,4
  //   ,c,4,14,c,1c,8,24,14,2c,c,34,1c,3c,10,44,24,4c,14,54,2c,5c,18
  //   ,64,34,6c,1c,74,3c,7c,20,84,44,8c,24,94,4c,9c,28,a4,54,ac,2c,b4
  //   ,5c,bc,30,c4,64,cc,34,d4,6c,dc,38,e4,74,ec,3c,f4,7c,fc,40,104
  //   ,84,10c,44,114,8c,11c,48,124,94,12c,4c,134,9c,13c,50,144,a4,14c
  //   ,54,154,ac,15c,58,164,b4,16c,5c,174,bc,17c,60,184,c4,18c,64,194
  //   ,cc,19c,68,1a4,d4,1ac,6c,1b4,dc,1bc,70,1c4,e4,1cc,74,1d4,ec,1dc
  //   ,78,1e4,f4,1ec,7c,1f4,fc,1fc,80,204,104,20c,84,214,10c,21c,88
  //   ,224,114,22c,8c,234,11c,23c,90,244,124,24c,94,254,12c,25c,98,264
  //   ,134,26c,9c,274,13c,27c,a0,284,144,28c,a4,294,14c,29c,a8,2a4,154
  //   ,2ac,ac,2b4,15c,2bc,b0,2c4,164,2cc,b4,2d4,16c,2dc,b8,2e4,174,2ec
  //   ,bc,2f4,17c,2fc,c0,304,184,30c,c4,314,18c,31c,c8,324,194,32c,cc
  //   ,334,19c,33c,d0,344,1a4,34c,d4,354,1ac,35c,d8,364,1b4,36c,dc,374
  //   ,1bc,37c,e0,384,1c4,38c,e4,394,1cc,39c,e8,3a4,1d4,3ac,ec,3b4,1dc
  //   ,3bc,f0,3c4,1e4,3cc,f4,3d4,1ec,3dc,f8,3e4,1f4,3ec,fc,3f4,1fc,3fc
  //   ,0,5,a,f,14,5,1e,23,28,2d,a,37,3c,41,46,f,50,55,5a,5f,14,69,6e
  //   ,73,78,19,82,87,8c,91,1e,9b,a0,a5,aa,23,b4,b9,be,c3,28,cd,d2,d7
  //   ,dc,2d,e6,eb,f0,f5,32,ff,104,109,10e,37,118,11d,122,127,3c,131
  //   ,136,13b,140,41,14a,14f,154,159,46,163,168,16d,172,4b,17c,181
  //   ,186,18b,50,195,19a,19f,1a4,55,1ae,1b3,1b8,1bd,5a,1c7,1cc,1d1
  //   ,1d6,5f,1e0,1e5,1ea,1ef,64,1f9,1fe,203,208,69,212,217,21c,221
  //   ,6e,22b,230,235,23a,73,244,249,24e,253,78,25d,262,267,26c,7d,276
  //   ,27b,280,285,82,28f,294,299,29e,87,2a8,2ad,2b2,2b7,8c,2c1,2c6
  //   ,2cb,2d0,91,2da,2df,2e4,2e9,96,2f3,2f8,2fd,302,9b,30c,311,316
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endmodule
