// Digital circuit test.dig as structural Verilog
module test (
  input  start,
  input  in_3,
  output out_2
);

  wire and_1_out;

  and and_1 (and_1_out, start, ~out_2);  // And
  D_FF d_ff_1 (.D(and_1_out), .C(in_3), .Q(out_2));  // open: nQ
endmodule
